// Digital circuit 6502.dig as structural Verilog
module _6502 (
  input  [7:0] D_bus,
  input  [15:0] A_bus,
  input  CLK,
  output [7:0] A,
  output [7:0] X,
  output [7:0] Y,
  output [7:0] SP,
  output [15:0] PC,
  output [7:0] PS,
  output [7:0] IR,
  output [45:0] word,
  output [15:0] MAR
);

  wire and_1_out, any_bits__or_1_or, id_1_brk, not_1_out;
  wire [2:0] pulldown_1_out;
  wire [7:0] alu_1_f_out, undriven;
  wire [15:0] address_control_1_o;

  not not_1 (not_1_out, CLK);
  var_ring_counter_with_reset #(.generic("size := 8;")) var_ring_counter_with_reset_1 (.C(not_1_out), .R(word[45]));
  any_bits__or #(.generic("bits := 8;")) any_bits__or_1 (.d_n(undriven), .\or (any_bits__or_1_or));
  var_encoder #(.generic("bits := 3;")) var_encoder_1 ();
  ID id_1 (.I(IR), .C(pulldown_1_out), .EN(any_bits__or_1_or), .F(PS), .O(word), .BRK(id_1_brk));
  PullDown #(.Bits(3)) pulldown_1 (.out(pulldown_1_out));
  PC #(.generic("init := 0; if(isPresent(args.pc)) init = args.pc;")) pc_1 (
    .RE(word[37]), .BCH(word[40]), .JMP(word[38]), .INC(word[39]), .C(CLK), .D_a(A_bus), .Q(PC),
    .LRE(word[41]), .LWE(word[42]), .HRE(word[43]), .HWE(word[44]), .D_d(D_bus));
  LO_MAR lo_mar_1 (
    .D_A(A_bus[7:0]), .A_RE(word[17]), .A_WE(word[18]), .C(CLK), .CLR(word[21]), .D_D(D_bus),
    .D_RE(word[19]), .D_WE(word[20]), .Q(MAR[7:0]));
  HI_MAR hi_mar_1 (
    .D_A(A_bus[15:8]), .A_RE(word[17]), .A_WE(word[18]), .C(CLK), .CLR(word[24]), .D_D(D_bus),
    .D_RE(word[22]), .D_WE(word[23]), .Q(MAR[15:8]));
  address_control address_control_1 (.M(word[30:27]), .A(A_bus), .X(X), .Y(Y), .O(address_control_1_o));
  SP sp_1 (
    .INC(word[33]), .DEC(word[34]), .D_RE(word[35]), .D_WE(word[36]), .D_D(D_bus), .Q(SP), .C(CLK),
    .A_RE(word[31]), .A_WE(word[32]), .D_A(A_bus));
  and and_1 (and_1_out, id_1_brk, undriven[0], CLK);
  Break break_1 (.brk(and_1_out));
  RAM #(.generic("data := []; if(isPresent(args.data)) data = args.data;")) ram_1 (
    .A(address_control_1_o), .C(CLK), .RE(word[25]), .WE(word[26]), .D(D_bus));
  PS ps_1 (.D_D(D_bus), .C(CLK), .F_out(PS), .D_RE(word[14]), .D_WE(word[15]), .F_in(alu_1_f_out), .A_WE(word[7]));
  ALU alu_1 (
    .F_in(PS), .A(A), .X(X), .Y(Y), .D(D_bus), .F_out(alu_1_f_out), .RE(word[6]), .WE(word[7]), .CLK(CLK),
    .OP(word[13:8]));
  A a_1 (.RE(word[0]), .WE(word[1]), .C(CLK), .Q(A), .D(D_bus));
  X x_1 (.RE(word[2]), .WE(word[3]), .C(CLK), .Q(X), .D(D_bus));
  Y y_1 (.RE(word[4]), .WE(word[5]), .C(CLK), .Q(Y), .D(D_bus));
  IR ir_1 (.WE(word[16]), .C(CLK), .Q(IR), .D(D_bus));

  // Notes on the sheet:
  //   CLK: Hz: 2147483647
endmodule

/* Code that sets the parameters or builds the circuit:
pc := 0;
data := [];
*/
