// Digital circuit base.dig as structural Verilog
module base (
  input  clk
);

  wire [7:0] A, DBUS, IR, PS, SP, X, Y;
  wire [15:0] ABUS, MAR, PC;

  _6502 #(.generic("pc := 0x0600; data := [ 0,0,0,0,0,0,0,0,0,0,0,0,0,0,0,0,0,0,0,0,0,0,0,0,0,0,0,0,0,0,0,0,0,0,0,0,0,0,0,0,0,0,0,0,0,0,0,0,0,0,0,0,0,0,0,0,0,0,0,0,0,0,0,0,0,0,0,0,0,0,0,0,0,0,0,0,0,0,0,0,0,0,0,0,0,0,0,0,0,0,0,0,0,0,0,0,0,0,0,0,0,0,0,0,0,0,0,0,0,0,0,0,0,0,0,0,0,0,0,0,0,0,0,0,0,0,0,0,0,0,0,0,0,0,0,0,0,0,0,0,0,0,0,0,0,0,0,0,0,0,0,0,0,0,0,0,0,0,0,0,0,0,0,0,0,0,0,0,0,0,0,0,0,0,0,0,0,0,0,0,0,0,0,0,0,0,0,0,")) _6502_1 (
    .PC(PC), .MAR(MAR), .SP(SP), .D_bus(DBUS), .A_bus(ABUS), .CLK(clk), .A(A), .X(X), .Y(Y), .PS(PS), .IR(IR));  // open: word
  // Probe on A
  // Probe on SP
  // Probe on PS
  // Probe on ABUS
  // Probe on X
  // Probe on Y
  // Probe on PC
  // Probe on IR
  // Probe on DBUS
endmodule
