// Digital circuit ALU.dig as structural Verilog
// arithemitic logic unit
module ALU (
  input  [7:0] F_in,
  input  RE,
  input  WE,
  input  CLK,
  input  [5:0] OP,
  input  [7:0] A,
  input  [7:0] X,
  input  [7:0] Y,
  input  [7:0] D,
  output [7:0] F_out
);

  wire var_multiplexer_1_p4, xor_2_out, xor_3_out, xor_4_out, xor_5_out;
  wire [1:1] no_bits__nor_10_nor, no_bits__nor_11_nor, no_bits__nor_12_nor, no_bits__nor_13_nor,
       no_bits__nor_14_nor;
  wire [6:0] var_adder_1_c_o, var_adder_5_out_4;
  wire [7:0] and_1_out, not_1_out, not_3_out, var_adder_1_out_4, var_multiplexer_2_p4, var_multiplexer_3_p4,
       var_reg_with_init_1_p21;
  wire [15:0] var_adder_2_out_4, var_adder_5_c_o, var_multiplexer_4_p5;
  wire [15:1] and_2_out, not_4_out, or_1_out, var_adder_3_out_4, xor_1_out;

  // var_multiplexer #(.generic("data_bits := 8; sel_bits := 1; sel_pos := \"top\";")) var_multiplexer_1: pin names not known; wires that end beside it: OP[2], X, Y, var_multiplexer_1_p4
  // var_multiplexer #(.generic("data_bits := 8; sel_bits := 1; sel_pos := \"top\";")) var_multiplexer_2: pin names not known; wires that end beside it: OP[3], var_multiplexer_1_p4, D, var_multiplexer_2_p4
  // var_multiplexer #(.generic("data_bits := 8; sel_bits := 1; sel_pos := \"top\";")) var_multiplexer_3: pin names not known; wires that end beside it: OP[3], var_multiplexer_1_p4, A, var_multiplexer_3_p4
  // var_multiplexer #(.generic("data_bits := 8; sel_bits := 1; sel_pos := \"top\";")) var_multiplexer_4: pin names not known; wires that end beside it: X, OP[0], A, D, {var_multiplexer_4_p5[0], var_multiplexer_4_p5[15:9]}
  assign not_1_out = ~D;  // Not not_1, 8 bits wide
  // Not not_2 has open pins: in=var_multiplexer_2_p4, out=open
  assign not_3_out = ~D;  // Not not_3, 8 bits wide
  assign and_1_out = A & D;  // And and_1, 8 bits wide
  var_adder #(.generic("bits := 8;")) var_adder_1 (
    .A(A), .B(D), .c_i(F_in[0]), .out_4(var_adder_1_out_4), .c_o(var_adder_1_c_o[0]));
  var_adder #(.generic("bits := 8;")) var_adder_2 (
    .A(A), .B(not_1_out), .c_i(F_in[0]), .out_4(var_adder_2_out_4[15:8]), .c_o(var_adder_2_out_4[0]));
  var_adder #(.generic("bits := 8;")) var_adder_3 (
    .A(var_multiplexer_2_p4), .c_i(1'b1), .out_4(var_adder_3_out_4[15:8]));  // open: B, c_o
  // var_adder #(.generic("bits := 8;")) var_adder_4: pin names not known; wires that end beside it: 1'b1
  // Not not_4 has open pins: in=open, out=not_4_out[15:8]
  var_adder #(.generic("bits := 8;")) var_adder_5 (
    .A(var_multiplexer_3_p4), .B(not_3_out), .c_i(1'b1), .out_4({var_adder_5_c_o[7], var_adder_5_out_4}),
    .c_o(var_adder_5_c_o[0]));
  assign and_2_out[15:8] = A & D;  // And and_2, 8 bits wide
  assign or_1_out[15:8] = A | D;  // Or or_1, 8 bits wide
  assign xor_1_out[15:8] = A ^ D;  // XOr xor_1, 8 bits wide
  no_bits__nor #(.generic("bits := 8;")) no_bits__nor_1 (.d_n(var_adder_1_out_4), .\nor (var_adder_1_c_o[1]));
  no_bits__nor #(.generic("bits := 8;")) no_bits__nor_2 (.d_n(var_adder_2_out_4[15:8]), .\nor (var_adder_2_out_4[1]));
  no_bits__nor #(.generic("bits := 8;")) no_bits__nor_3 (
    .d_n({var_adder_5_c_o[7], var_adder_5_out_4}), .\nor (var_adder_5_c_o[1]));
  xor xor_2 (xor_2_out, X[7], A[7]);
  and and_3 (var_adder_1_c_o[6], xor_2_out, xor_3_out);
  xor xor_3 (xor_3_out, A[7], var_adder_1_out_4[7]);
  xor xor_4 (xor_4_out, X[7], A[7]);
  and and_4 (var_adder_2_out_4[6], xor_4_out, xor_5_out);
  xor xor_5 (xor_5_out, A[7], var_adder_2_out_4[15]);
  no_bits__nor #(.generic("bits := 8;")) no_bits__nor_4 (.d_n(var_adder_3_out_4[15:8]), .\nor (var_adder_3_out_4[1]));
  no_bits__nor #(.generic("bits := 8;")) no_bits__nor_5 (.d_n(not_4_out[15:8]), .\nor (not_4_out[1]));
  no_bits__nor #(.generic("bits := 8;")) no_bits__nor_6 (.d_n(and_2_out[15:8]), .\nor (and_2_out[1]));
  no_bits__nor #(.generic("bits := 8;")) no_bits__nor_7 (.d_n(or_1_out[15:8]), .\nor (or_1_out[1]));
  no_bits__nor #(.generic("bits := 8;")) no_bits__nor_8 (.d_n(xor_1_out[15:8]), .\nor (xor_1_out[1]));
  no_bits__nor #(.generic("bits := 8;")) no_bits__nor_9 (
    .d_n({var_multiplexer_4_p5[15:9], 1'b0}), .\nor (var_multiplexer_4_p5[1]));
  no_bits__nor #(.generic("bits := 8;")) no_bits__nor_10 (
    .d_n({1'b0, var_multiplexer_4_p5[0], var_multiplexer_4_p5[15:10]}), .\nor (no_bits__nor_10_nor[1]));
  no_bits__nor #(.generic("bits := 8;")) no_bits__nor_11 (
    .d_n({var_multiplexer_4_p5[15:9], F_in[0]}), .\nor (no_bits__nor_11_nor[1]));
  no_bits__nor #(.generic("bits := 8;")) no_bits__nor_12 (
    .d_n({F_in[0], var_multiplexer_4_p5[0], var_multiplexer_4_p5[15:10]}), .\nor (no_bits__nor_12_nor[1]));
  no_bits__nor #(.generic("bits := 8;")) no_bits__nor_13 (.d_n(and_1_out), .\nor (no_bits__nor_13_nor[1]));
  no_bits__nor #(.generic("bits := 8;")) no_bits__nor_14 (.d_n(D), .\nor (no_bits__nor_14_nor[1]));
  // var_multiplexer #(.generic("data_bits := 16; sel_bits := 6; sel_pos := \"top\";")) var_multiplexer_5: pin names not known; wires that end beside it: OP, {var_adder_1_out_4, var_adder_1_out_4[7], var_adder_1_c_o[6], F_in[5:2], var_adder_1_c_o[1:0]}, {var_adder_5_c_o[15:7], F_in[6:2], var_adder_5_c_o[1:0]}, {var_adder_3_out_4[15:8], var_adder_3_out_4[15], F_in[6:2], var_adder_3_out_4[1], F_in[0]}, {not_4_out[15:8], not_4_out[15], F_in[6:2], not_4_out[1], F_in[0]}, {var_adder_5_c_o[15:7], F_in[6:2], var_adder_5_c_o[1:0]}, {var_adder_2_out_4[15:8], var_adder_2_out_4[15], var_adder_2_out_4[6], F_in[5:2], var_adder_2_out_4[1:0]}, {var_adder_3_out_4[15:8], var_adder_3_out_4[15], F_in[6:2], var_adder_3_out_4[1], F_in[0]}, {not_4_out[15:8], not_4_out[15], F_in[6:2], not_4_out[1], F_in[0]}, {var_adder_5_c_o[15:7], F_in[6:2], var_adder_5_c_o[1:0]}, {var_adder_3_out_4[15:8], var_adder_3_out_4[15], F_in[6:2], var_adder_3_out_4[1], F_in[0]}, {not_4_out[15:8], not_4_out[15], F_in[6:2], not_4_out[1], F_in[0]}, {and_2_out[15:8], and_2_out[15], F_in[6:2], and_2_out[1], F_in[0]}, {or_1_out[15:8], or_1_out[15], F_in[6:2], or_1_out[1], F_in[0]}, {xor_1_out[15:8], xor_1_out[15], F_in[6:2], xor_1_out[1], F_in[0]}, {var_multiplexer_4_p5[15:9], 1'b0, var_multiplexer_4_p5[15], F_in[6:2], var_multiplexer_4_p5[1:0]}, {var_multiplexer_4_p5[15:9], 1'b0, var_multiplexer_4_p5[15], F_in[6:2], var_multiplexer_4_p5[1:0]}, {1'b0, var_multiplexer_4_p5[0], var_multiplexer_4_p5[15:10], 1'b0, F_in[6:2], no_bits__nor_10_nor[1], var_multiplexer_4_p5[9]}, {1'b0, var_multiplexer_4_p5[0], var_multiplexer_4_p5[15:10], 1'b0, F_in[6:2], no_bits__nor_10_nor[1], var_multiplexer_4_p5[9]}, {var_multiplexer_4_p5[15:9], F_in[0], var_multiplexer_4_p5[15], F_in[6:2], no_bits__nor_11_nor[1], var_multiplexer_4_p5[0]}, {var_multiplexer_4_p5[15:9], F_in[0], var_multiplexer_4_p5[15], F_in[6:2], no_bits__nor_11_nor[1], var_multiplexer_4_p5[0]}, {F_in[0], var_multiplexer_4_p5[0], var_multiplexer_4_p5[15:10], F_in[0], F_in[6:2], no_bits__nor_12_nor[1], var_multiplexer_4_p5[9]}, {F_in[0], var_multiplexer_4_p5[0], var_multiplexer_4_p5[15:10], F_in[0], F_in[6:2], no_bits__nor_12_nor[1], var_multiplexer_4_p5[9]}, {var_adder_5_c_o[15:8], F_in[7:1], OP[0]}
  // var_reg_with_init #(.generic("bits := 8; init := 0;")) var_reg_with_init_1: pin names not known; wires that end beside it: {var_adder_5_c_o[15:8], F_in[7:1], OP[0]}, {var_adder_5_c_o[15:8], F_in[7:4], OP[0], F_in[2:0]}, {var_adder_5_c_o[15:8], F_in[7:4], OP[0], F_in[2:0]}, {var_adder_5_c_o[15:8], F_in[7:3], OP[0], F_in[1:0]}, {var_adder_5_c_o[15:8], F_in[7:3], OP[0], F_in[1:0]}, {var_adder_5_c_o[15:8], F_in[7], 1'b0, F_in[5:0]}, {var_adder_5_c_o[15:8], D[7:6], F_in[5:2], no_bits__nor_13_nor[1], F_in[0]}, {16{1'b0}}, {var_adder_5_c_o[15:8], D[7], F_in[6:2], no_bits__nor_14_nor[1], F_in[0]}, {16{1'b0}}, {16{1'b0}}, {16{1'b0}}, {16{1'b0}}, {16{1'b0}}, {16{1'b0}}, {16{1'b0}}, {16{1'b0}}, 1'b0, WE, CLK, var_reg_with_init_1_p21, var_adder_5_c_o[15:8]
  assign D = RE ? var_adder_5_c_o[15:8] : 8'bz;  // Driver driver_1

  // Notes on the sheet:
  //   F_in: flags in
  //   RE: read enable
  //   WE: write enable
  //   F_out: flags out
  //   OP: op-code
  //   A: A register
  //   X: X register
  //   Y: Y register
  //   D: data in/out
  //   ADC
  //   SBC
  //   CMP
  //   INC
  //   DEC
  //   AND
  //   ORA
  //   EOR
  //   ASL
  //   LSR
  //   ROL
  //   ROR
  //   0 : ADC
  //   1 : CPX
  //   2 : INX
  //   3 : DEX
  //   4 : CPY
  //   5 : SBC
  //   6 : INY
  //   7 : DEY
  //   8 : CMP
  //   9 : INC
  //   10 : DEC
  //   11 : AND
  //   12 : ORA
  //   13 : EOR
  //   14 : ASL A
  //   15 : ASL M
  //   16 : LSR A
  //   17 : LSR M
  //   18 : ROL A
  //   19 : ROL M
  //   20 : ROR A
  //   21 : ROR M
  //   22 : CLC
  //   23 : SEC
  //   24 : CLD
  //   25 : SED
  //   26 : CLI
  //   27 : SEI
  //   28 : CLV
  //   29 : BIT
  //   ADC
  //   SBC
  //   INC
  //   DEC
  //   CMP
  //   AND
  //   ORA
  //   EOR
  //   ASL
  //   LSR
  //   ROL
  //   CLC
  //   CLI
  //   CLV
  //   BIT
  //   FLGS
  //   N
  //   V
  //   -
  //   B
  //   D
  //   I
  //   Z
  //   C
  //   N
  //   V
  //   -
  //   B
  //   D
  //   I
  //   Z
  //   C
endmodule
