// Digital circuit HI MAR.dig as structural Verilog
// memory address register (high byte)
module HI_MAR (
  input  C,
  input  CLR,
  input  D_RE,
  input  D_WE,
  input  A_RE,
  input  A_WE,
  input  [7:0] D_A,
  input  [7:0] D_D,
  output [7:0] Q
);

  wire and_1_out, and_2_out, and_3_out, edge_pulse_detector_1_plus, or_1_out, xor_1_out;
  wire [7:0] driver_1_out, driverinvsel_1_out;

  or or_1 (or_1_out, CLR, xor_1_out);
  xor xor_1 (xor_1_out, D_WE, A_WE);
  and and_1 (and_1_out, or_1_out, edge_pulse_detector_1_plus);
  edge_pulse_detector edge_pulse_detector_1 (.clk(C), .plus(edge_pulse_detector_1_plus));
  and and_2 (and_2_out, ~D_WE, A_WE);  // And
  assign driver_1_out = and_2_out ? D_A : 8'bz;  // Driver driver_1
  assign D_A = A_RE ? Q : 8'bz;  // Driver driver_2
  assign driverinvsel_1_out = ~CLR ? driver_1_out : 8'bz;  // DriverInvSel driverinvsel_1
  assign driverinvsel_1_out = CLR ? {8{1'b0}} : 8'bz;  // Driver driver_3
  assign driver_1_out = and_3_out ? D_D : 8'bz;  // Driver driver_4
  assign D_D = D_RE ? Q : 8'bz;  // Driver driver_5
  // var_DFF_with_init #(.generic("bits := 8; init := 0;")) var_dff_with_init_1: pin names not known; wires that end beside it: driverinvsel_1_out, and_1_out, Q
  and and_3 (and_3_out, D_WE, ~A_WE);  // And
endmodule
