// Digital circuit ID.dig as structural Verilog
// instruction decode
module ID (
  input  [7:0] I,
  input  [2:0] C,
  input  EN,
  input  [7:0] F,
  output [45:0] O,
  output BRK
);

  wire all_bits__and_1_and, all_bits__and_2_and, all_bits__and_3_and, all_bits__and_4_and,
       all_bits__and_5_and, all_bits__and_6_and, all_bits__and_7_and, all_bits__and_8_and, and_1_out,
       and_2_out, and_3_out, and_4_out, and_5_out, and_6_out, and_7_out, and_8_out, no_bits__nor_1_nor,
       or_1_out;
  wire [7:0] xnor_1_out, xnor_2_out, xnor_3_out, xnor_4_out, xnor_5_out, xnor_6_out, xnor_7_out, xnor_8_out;
  wire [45:0] driver_1_out, lookuptable_1_out, lookuptable_2_out, lookuptable_3_out, lookuptable_4_out,
       lookuptable_5_out, lookuptable_6_out, lookuptable_7_out, var_multiplexer_1_p10;

  assign xnor_1_out = ~(I ^ 8'h10);  // XNOr xnor_1, 8 bits wide
  assign xnor_2_out = ~(I ^ 8'h30);  // XNOr xnor_2, 8 bits wide
  assign xnor_3_out = ~(I ^ 8'h50);  // XNOr xnor_3, 8 bits wide
  assign xnor_4_out = ~(I ^ 8'h70);  // XNOr xnor_4, 8 bits wide
  assign xnor_5_out = ~(I ^ 8'h90);  // XNOr xnor_5, 8 bits wide
  assign xnor_6_out = ~(I ^ 8'hb0);  // XNOr xnor_6, 8 bits wide
  assign xnor_7_out = ~(I ^ 8'hd0);  // XNOr xnor_7, 8 bits wide
  assign xnor_8_out = ~(I ^ 8'hf0);  // XNOr xnor_8, 8 bits wide
  all_bits__and #(.generic("bits := 8;")) all_bits__and_1 (.d_n(xnor_1_out), .\and (all_bits__and_1_and));
  all_bits__and #(.generic("bits := 8;")) all_bits__and_2 (.d_n(xnor_2_out), .\and (all_bits__and_2_and));
  all_bits__and #(.generic("bits := 8;")) all_bits__and_3 (.d_n(xnor_3_out), .\and (all_bits__and_3_and));
  all_bits__and #(.generic("bits := 8;")) all_bits__and_4 (.d_n(xnor_4_out), .\and (all_bits__and_4_and));
  all_bits__and #(.generic("bits := 8;")) all_bits__and_5 (.d_n(xnor_5_out), .\and (all_bits__and_5_and));
  all_bits__and #(.generic("bits := 8;")) all_bits__and_6 (.d_n(xnor_6_out), .\and (all_bits__and_6_and));
  all_bits__and #(.generic("bits := 8;")) all_bits__and_7 (.d_n(xnor_7_out), .\and (all_bits__and_7_and));
  all_bits__and #(.generic("bits := 8;")) all_bits__and_8 (.d_n(xnor_8_out), .\and (all_bits__and_8_and));
  and and_1 (and_1_out, all_bits__and_1_and, F[7]);
  and and_2 (and_2_out, all_bits__and_2_and, ~F[7]);  // And
  and and_3 (and_3_out, all_bits__and_3_and, F[6]);
  and and_4 (and_4_out, all_bits__and_4_and, ~F[6]);  // And
  and and_5 (and_5_out, all_bits__and_5_and, F[0]);
  and and_6 (and_6_out, all_bits__and_6_and, ~F[0]);  // And
  and and_7 (and_7_out, all_bits__and_7_and, F[1]);
  and and_8 (and_8_out, all_bits__and_8_and, ~F[1]);  // And
  no_bits__nor #(.generic("bits := 8;")) no_bits__nor_1 (.d_n(I), .\nor (no_bits__nor_1_nor));
  or or_1 (or_1_out, and_1_out, and_2_out, and_3_out, and_4_out, and_5_out, and_6_out, and_7_out, and_8_out);
  LookUpTable #(.Bits(46)) lookuptable_1 (
    .in0(I[0]), .in1(I[1]), .in2(I[2]), .in3(I[3]), .in4(I[4]), .in5(I[5]), .in6(I[6]), .in7(I[7]),
    .out(lookuptable_1_out));
  LookUpTable #(.Bits(46)) lookuptable_2 (
    .in0(I[0]), .in1(I[1]), .in2(I[2]), .in3(I[3]), .in4(I[4]), .in5(I[5]), .in6(I[6]), .in7(I[7]),
    .out(lookuptable_2_out));
  LookUpTable #(.Bits(46)) lookuptable_3 (
    .in0(I[0]), .in1(I[1]), .in2(I[2]), .in3(I[3]), .in4(I[4]), .in5(I[5]), .in6(I[6]), .in7(I[7]),
    .out(lookuptable_3_out));
  LookUpTable #(.Bits(46)) lookuptable_4 (
    .in0(I[0]), .in1(I[1]), .in2(I[2]), .in3(I[3]), .in4(I[4]), .in5(I[5]), .in6(I[6]), .in7(I[7]),
    .out(lookuptable_4_out));
  LookUpTable #(.Bits(46)) lookuptable_5 (
    .in0(I[0]), .in1(I[1]), .in2(I[2]), .in3(I[3]), .in4(I[4]), .in5(I[5]), .in6(I[6]), .in7(I[7]),
    .out(lookuptable_5_out));
  LookUpTable #(.Bits(46)) lookuptable_6 (
    .in0(I[0]), .in1(I[1]), .in2(I[2]), .in3(I[3]), .in4(I[4]), .in5(I[5]), .in6(I[6]), .in7(I[7]),
    .out(lookuptable_6_out));
  LookUpTable #(.Bits(46)) lookuptable_7 (
    .in0(I[0]), .in1(I[1]), .in2(I[2]), .in3(I[3]), .in4(I[4]), .in5(I[5]), .in6(I[6]), .in7(I[7]),
    .out(lookuptable_7_out));
  assign driver_1_out = or_1_out ? 46'h202000000000 : 46'bz;  // Driver driver_1
  assign driver_1_out = ~or_1_out ? lookuptable_1_out : 46'bz;  // DriverInvSel driverinvsel_1
  // var_multiplexer #(.generic("data_bits := 46; sel_bits := 3; sel_pos := \"top\";")) var_multiplexer_1: pin names not known; wires that end beside it: C, 46'ha002010000, driver_1_out, lookuptable_2_out, lookuptable_3_out, lookuptable_4_out, lookuptable_5_out, lookuptable_6_out, lookuptable_7_out, var_multiplexer_1_p10
  and and_9 (BRK, no_bits__nor_1_nor, EN);
  assign O = ~EN ? {46{1'b0}} : 46'bz;  // DriverInvSel driverinvsel_2
  assign O = EN ? var_multiplexer_1_p10 : 46'bz;  // Driver driver_2

  // Notes on the sheet:
  //   I: instruction op-code
  //   C: clock
  //   O: control word out
  //   EN: enable
  //   BRK: break
  //   F: flags
  //   contents of lookuptable_1 (hex, n*v repeats v):
  //   200000000000,2003100000,0,0,0,2003100000,2003100000,0,200484004000
  //   ,2002000c80,e80,0,0,2002100000,2002100000,0,2003100000,2003100000
  //   ,0,0,0,2003100000,2003100000,0,200000001680,2002100000,0,0,0,2002100000,2002100000
  //   ,0,2002100000,2003100000,0,0,2003100000,2003100000,2003100000
  //   ,0,200000000,2002000b80,1280,0,2002100000,2002100000,2002100000
  //   ,0,2003100000,2003100000,0,0,0,2003100000,2003100000,0,200000001780
  //   ,2002100000,0,0,0,2002100000,2002100000,0,200000000,2003100000
  //   ,0,0,0,2003100000,2003100000,0,200484000001,2002000d80,1080,0
  //   ,2002100000,2002100000,2002100000,0,2003100000,2003100000,0,0,0
  //   ,2003100000,2003100000,0,200000001a80,2002100000,0,0,0,2002100000,2002100000
  //   ,0,200000000,2003100000,0,0,0,2003100000,2003100000,0,200000000
  //   ,2002000080,1480,0,2002100000,2002100000,2002100000,0,2003100000,2003100000
  //   ,0,0,0,2003100000,2003100000,0,200000001b80,2002100000,0,0,0,2002100000,2002100000
  //   ,0,0,2003100000,0,0,2003100000,2003100000,2003100000,0,780,0,200000000006
  //   ,0,2002100000,2002100000,2002100000,0,2003100000,2003100000,0,0
  //   ,2003100000,2003100000,2003100000,0,200000000012,2002100000,201000000004
  //   ,0,0,2002100000,0,0,202002001fa0,2003100000,202002001f88,0,2003100000,2003100000,2003100000
  //   ,0,200000000021,202002001f82,200000000009,0,2002100000,2002100000,2002100000
  //   ,0,2003100000,2003100000,0,0,2003100000,2003100000,2003100000
  //   ,0,200000001c80,2002100000,200800000008,0,2002100000,2002100000,2002100000
  //   ,0,202002000480,2003100000,0,0,2003100000,2003100000,2003100000
  //   ,0,680,202002000880,380,0,2002100000,2002100000,2002100000,0,2003100000,2003100000
  //   ,0,0,0,2003100000,2003100000,0,200000001880,2002100000,0,0,0,2002100000,2002100000
  //   ,0,202002000180,2003100000,0,0,2003100000,2003100000,2003100000
  //   ,0,280,2002000580,200000000000,0,2002100000,2002100000,2002100000
  //   ,0,2003100000,2003100000,0,0,0,2003100000,2003100000,0,200000001980
  //   ,2002100000,0,0,0,2002100000,2002100000
  //   contents of lookuptable_2 (hex, n*v repeats v):
  //   80484000000,2a820000,0,0,0,2020c80,2020f80,0,0,200000000042,200000000042
  //   ,0,0,2002800000,2002800000,0,214000020000,32820000,0,0,0,a020c80
  //   ,a020f80,0,0,2002800000,0,0,0,2002800000,2002800000,0,2002800000
  //   ,2a820000,0,0,200002021d80,2020b80,2021380,0,200082008000,200000000042,200000000042
  //   ,0,2002800000,2002800000,2002800000,0,214000020000,32820000,0,0,0
  //   ,a020b80,a021380,0,0,2002800000,0,0,0,2002800000,2002800000,0
  //   ,282008000,2a820000,0,0,0,2020d80,2021180,0,0,200000000042,200000000042
  //   ,0,2002800000,2002800000,2002800000,0,214000020000,32820000,0,0,0
  //   ,a020d80,a021180,0,0,2002800000,0,0,0,2002800000,2002800000,0
  //   ,282100000,2a820000,0,0,0,2020080,2021580,0,200082001f82,200000000042,200000000042
  //   ,0,2002800000,2002800000,2002800000,0,214000020000,32820000,0,0,0
  //   ,a020080,a021580,0,0,2002800000,0,0,0,2002800000,2002800000,0,0
  //   ,2a820000,0,0,200004020010,200004020001,200004020004,0,200000000060
  //   ,0,0,0,2002800000,2002800000,2002800000,0,214000020000,32820000
  //   ,0,0,20000c020010,20000c020001,200014020004,0,0,2002800000,0,0,0
  //   ,2002800000,0,0,0,2a820000,0,0,200002021fa0,200002021f82,200002021f88
  //   ,5*0,2002800000,2002800000,2002800000,0,214000020000,32820000
  //   ,0,0,20000a021fa0,20000a021f82,200012021f88,0,0,2002800000,0,0
  //   ,2002800000,2002800000,2002800000,0,0,2a820000,0,0,200002020480
  //   ,200002020880,2020a80,0,200000000060,0,200000000048,0,2002800000,2002800000,2002800000
  //   ,0,214000020000,32820000,0,0,0,20000a020880,a020a80,0,0,2002800000
  //   ,0,0,0,2002800000,2002800000,0,0,2a820000,0,0,200002020180,2020580
  //   ,2020980,0,200000000048,200000000042,0,0,2002800000,2002800000,2002800000
  //   ,0,214000020000,32820000,0,0,0,a020580,a020980,0,0,2002800000
  //   ,0,0,0,2002800000,2002800000
  //   contents of lookuptable_3 (hex, n*v repeats v):
  //   220484000000,a120000,0,0,0,200000000042,200004020040,6*0,2020c80
  //   ,2020f80,0,0,3a120000,0,0,0,200000000042,20000c020040,0,0,22020c80
  //   ,0,0,0,1a020c80,1a020f80,0,80484000000,a120000,0,0,0,200000000042
  //   ,200004020040,5*0,200002021d80,2020b80,2021380,0,0,3a120000,0,0,0
  //   ,200000000042,20000c020040,0,0,22020b80,0,0,0,1a020b80,1a021380
  //   ,0,40282000000,a120000,0,0,0,200000000042,200004020040,5*0,204000020000
  //   ,2020d80,2021180,0,0,3a120000,0,0,0,200000000042,20000c020040
  //   ,0,0,22020d80,0,0,0,1a020d80,1a021180,0,82800000,a120000,0,0,0
  //   ,200000000042,200004020040,5*0,4000020000,2020080,2021580,0,0
  //   ,3a120000,0,0,0,200000000042,20000c020040,0,0,22020080,0,0,0,1a020080
  //   ,1a021580,0,0,a120000,10*0,200004020010,200004020001,200004020004
  //   ,0,0,3a120000,7*0,200024020001,0,0,0,20001c020001,0,0,0,a120000
  //   ,10*0,200002021fa0,200002021f82,200002021f88,0,0,3a120000,7*0
  //   ,200022021f82,0,0,20001a021fa0,20001a021f82,200022021f88,0,0,a120000
  //   ,4*0,200004020040,5*0,200002020480,200002020880,2020a80,0,0,3a120000
  //   ,4*0,20000c020040,0,0,200022020880,0,0,0,20001a020880,1a020a80
  //   ,0,0,a120000,0,0,0,200000000042,200004020040,5*0,200002020180
  //   ,2020580,2020980,0,0,3a120000,0,0,0,200000000042,20000c020040
  //   ,0,0,22020580,0,0,0,1a020580,1a020980
  //   contents of lookuptable_4 (hex, n*v repeats v):
  //   0,2020c80,11*0,200000000042,200004020040,0,0,22020c80,7*0,200000000042
  //   ,0,0,0,200000000042,20001c020040,0,20484000000,2020b80,11*0,200000000042
  //   ,200004020040,0,0,22020b80,7*0,200000000042,0,0,0,200000000042
  //   ,20001c020040,0,300082000000,2020d80,11*0,200000000042,200004020040
  //   ,0,0,22020d80,7*0,200000000042,0,0,0,200000000042,20001c020040
  //   ,0,204000020000,2020080,10*0,2002100000,200000000042,200004020040
  //   ,0,0,22020080,7*0,200000000042,0,0,0,200000000042,20001c020040
  //   ,0,0,200004020001,15*0,200024020001,15*0,200002021f82,15*0,200022021f82
  //   ,15*0,200002020880,12*0,200004020040,0,0,200022020880,12*0,20001c020040
  //   ,0,0,2020580,11*0,200000000042,200004020040,0,0,22020580,7*0,200000000042
  //   ,0,0,0,200000000042,20001c020040
  //   contents of lookuptable_5 (hex, n*v repeats v):
  //   0,200000000042,15*0,200000000042,14*0,204000020000,200000000042
  //   ,15*0,200000000042,15*0,200000000042,15*0,200000000042,15*0,200000000042
  //   ,10*0,2002800000,4*0,200000000042,111*0,200000000042,15*0,200000000042
  //   contents of lookuptable_6 (hex, n*v repeats v):
  //   108*0,204000020000
endmodule
