// Digital circuit IR.dig as structural Verilog
// instruction register
module IR (
  input  WE,
  input  [7:0] D,
  input  C,
  output [7:0] Q
);

  wire and_1_out, edge_pulse_detector_1_plus;

  and and_1 (and_1_out, WE, edge_pulse_detector_1_plus);
  edge_pulse_detector edge_pulse_detector_1 (.clk(C), .plus(edge_pulse_detector_1_plus));
  // var_DFF_with_init #(.generic("bits := 8; init := 0;")) var_dff_with_init_1: pin names not known; wires that end beside it: D, and_1_out, Q

  // Notes on the sheet:
  //   WE: write enable
  //   D: data in/out
  //   Q: data out
endmodule
