// Digital circuit PC.dig as structural Verilog
// program counter
module PC (
  input  RE,
  input  JMP,
  input  INC,
  input  C,
  input  [15:0] D_a,
  input  BCH,
  input  LRE,
  input  LWE,
  input  HRE,
  input  HWE,
  input  [7:0] D_d,
  output [15:0] Q
);

  wire and_1_out, and_2_out, and_3_out, edge_pulse_detector_1_plus, or_1_out, or_2_out, or_3_out, or_4_out;
  wire [15:0] driver_1_out, driver_2_out, driver_4_out, driver_6_out, driver_10_out, driverinvsel_1_out,
       driverinvsel_2_out, var_adder_1_p4, var_adder_2_p3;

  and and_1 (and_1_out, BCH, JMP);
  and and_2 (and_2_out, ~BCH, JMP);  // And
  edge_pulse_detector edge_pulse_detector_1 (.clk(C), .plus(edge_pulse_detector_1_plus));
  or or_1 (or_1_out, INC, RE);
  or or_2 (or_2_out, or_1_out, and_1_out, and_2_out);
  or or_3 (or_3_out, or_2_out, or_4_out);
  assign driver_1_out = and_1_out ? D_a : 16'bz;  // Driver driver_1
  assign driver_2_out = and_2_out ? D_a : 16'bz;  // Driver driver_2
  and and_3 (and_3_out, or_3_out, edge_pulse_detector_1_plus);
  assign driverinvsel_1_out = ~or_2_out ? driver_4_out : 16'bz;  // DriverInvSel driverinvsel_1
  assign D_a = RE ? Q : 16'bz;  // Driver driver_3
  assign driver_4_out = HWE ? {D_d, Q[7:0]} : 16'bz;  // Driver driver_4
  assign driver_4_out = LWE ? {Q[15:8], D_d} : 16'bz;  // Driver driver_5
  assign driverinvsel_2_out = ~or_4_out ? driver_2_out : 16'bz;  // DriverInvSel driverinvsel_2
  assign driver_6_out = or_2_out ? driverinvsel_2_out : 16'bz;  // Driver driver_6
  assign driver_6_out = or_4_out ? driverinvsel_1_out : 16'bz;  // Driver driver_7
  assign driver_2_out = ~and_2_out ? driver_10_out : 16'bz;  // DriverInvSel driverinvsel_3
  var_DFF_with_init #(.generic("bits := 16; init := args.init;")) var_dff_with_init_1 (
    .D(driver_6_out), .clk(and_3_out), .Q(Q));  // open: nQ
  assign D_d = LRE ? Q[7:0] : 8'bz;  // Driver driver_8
  assign D_d = HRE ? Q[15:8] : 8'bz;  // Driver driver_9
  // var_adder #(.generic("bits := 16;")) var_adder_1: pin names not known; wires that end beside it: and_2_out, Q, {{9{driver_1_out[7]}}, driver_1_out[6:0]}, var_adder_1_p4
  // var_adder #(.generic("bits := 16;")) var_adder_2: pin names not known; wires that end beside it: Q, 1'b1, var_adder_2_p3
  or or_4 (or_4_out, HWE, LWE);
  assign driver_10_out = and_1_out ? var_adder_1_p4 : 16'bz;  // Driver driver_10
  assign driver_10_out = ~and_1_out ? var_adder_2_p3 : 16'bz;  // DriverInvSel driverinvsel_4

  // Notes on the sheet:
  //   RE: read enable
  //   JMP: jump
  //   INC: increment
  //   D_a: data in/out
  //   Q: data out
  //   BCH: branch
  //   LRE: read enable
  //   LWE: branch
  //   HRE: read enable
  //   HWE: branch
  //   D_d: data in/out
endmodule

/* Code that sets the parameters or builds the circuit:
init := 0x0600;
*/
