// Digital circuit PS.dig as structural Verilog
// processor status (flags)
module PS (
  input  C,
  input  D_RE,
  input  D_WE,
  input  A_WE,
  input  [7:0] F_in,
  input  [7:0] D_D,
  output [7:0] F_out
);

  wire and_1_out, and_2_out, and_3_out, edge_pulse_detector_1_plus, xor_1_out;
  wire [7:0] driver_1_out;

  xor xor_1 (xor_1_out, A_WE, D_WE);
  and and_1 (and_1_out, xor_1_out, edge_pulse_detector_1_plus);
  edge_pulse_detector edge_pulse_detector_1 (.clk(C), .plus(edge_pulse_detector_1_plus));
  and and_2 (and_2_out, ~A_WE, D_WE);  // And
  assign driver_1_out = and_2_out ? D_D : 8'bz;  // Driver driver_1
  assign D_D = D_RE ? F_out : 8'bz;  // Driver driver_2
  assign driver_1_out = and_3_out ? F_in : 8'bz;  // Driver driver_3
  // var_DFF_with_init #(.generic("bits := 8; init := 0b00110000;")) var_dff_with_init_1: pin names not known; wires that end beside it: driver_1_out, and_1_out, F_out
  and and_3 (and_3_out, A_WE, ~D_WE);  // And
endmodule
