// Digital circuit RAM.dig as structural Verilog
// RAM with graphic display (0x200 - 0x5ff)
module RAM (
  input  [15:0] A,
  input  RE,
  input  WE,
  input  [7:0] D,
  input  C
);

  wire all_bits__and_1_and, all_bits__and_2_and, and_1_out, and_2_out, and_3_out, and_4_out, and_5_out,
       and_6_out, and_7_out, edge_pulse_detector_1_plus, nor_1_out, or_1_out, or_2_out, var_adder_1_p2,
       var_adder_2_p2;
  wire [6:0] kb_diode_relay_ver_1_key;
  wire [7:0] driver_1_out, eeprom_1_d, prng_1_r;
  wire [10:0] not_3_out;
  wire [15:0] xnor_1_out, xnor_2_out;
  wire [15:11] not_3_out_2;

  // Not not_1 has open pins: in=A, out=open
  // Not not_2 has open pins: in=16'h5ff, out=open
  and and_1 (and_1_out, all_bits__and_1_and, WE);
  // var_adder #(.generic("bits := 16;")) var_adder_1: pin names not known; wires that end beside it: 16'h200, var_adder_1_p2
  // Not not_3 has open pins: in=open, out={not_3_out_2, not_3_out}
  // var_adder #(.generic("bits := 16;")) var_adder_2: pin names not known; wires that end beside it: A, var_adder_2_p2
  assign xnor_1_out = ~(A ^ 16'hff);  // XNOr xnor_1, 16 bits wide
  assign xnor_2_out = ~(A ^ 16'hfe);  // XNOr xnor_2, 16 bits wide
  PRNG #(.Bits(8)) prng_1 (.S({8{1'b0}}), .se(1'b0), .ne(1'b1), .C(C), .R(prng_1_r));
  // Probe on {not_3_out_2, not_3_out}
  nor nor_1 (nor_1_out, var_adder_1_p2, var_adder_2_p2);
  all_bits__and #(.generic("bits := 16;")) all_bits__and_1 (.d_n(xnor_1_out), .\and (all_bits__and_1_and));
  kb_diode_relay_ver kb_diode_relay_ver_1 (.clk(C), .WE(and_1_out), .D(D), .key(kb_diode_relay_ver_1_key));
  all_bits__and #(.generic("bits := 16;")) all_bits__and_2 (.d_n(xnor_2_out), .\and (all_bits__and_2_and));
  and and_2 (and_2_out, WE, ~nor_1_out);  // And
  and and_3 (and_3_out, C, ~nor_1_out);  // And
  and and_4 (and_4_out, RE, ~nor_1_out);  // And
  and and_5 (and_5_out, nor_1_out, WE);
  and and_6 (and_6_out, nor_1_out, RE);
  assign driver_1_out = all_bits__and_1_and ? {1'b0, kb_diode_relay_ver_1_key} : 8'bz;  // Driver driver_1
  assign driver_1_out = all_bits__and_2_and ? prng_1_r : 8'bz;  // Driver driver_2
  or or_1 (or_1_out, and_4_out, and_2_out);
  and and_7 (and_7_out, and_2_out, edge_pulse_detector_1_plus);
  edge_pulse_detector edge_pulse_detector_1 (.clk(and_3_out), .plus(edge_pulse_detector_1_plus));
  EEPROM #(.AddrBits(16), .Bits(8), .generic("this.Data = args.data;")) eeprom_1 (
    .A(A), .CS(or_1_out), .WE(and_7_out), .OE(and_4_out), .D(eeprom_1_d));
  GraphicCard #(.graphicHeight(32), .graphicWidth(32), .Bits(8)) graphiccard_1 (
    .A(not_3_out), .str(and_5_out), .C(C), .ld(and_6_out), .B(1'b0), .D(eeprom_1_d));
  assign eeprom_1_d = WE ? D : 8'bz;  // Driver driver_3
  assign driver_1_out = ~or_2_out ? eeprom_1_d : 8'bz;  // DriverInvSel driverinvsel_1
  or or_2 (or_2_out, all_bits__and_1_and, all_bits__and_2_and);
  assign D = RE ? driver_1_out : 8'bz;  // Driver driver_4

  // Notes on the sheet:
  //   A: address
  //   RE: read enable
  //   WE: write enable
  //   D: data in/out
  //   C: Hz: 10
  //   contents of eeprom_1 (hex, n*v repeats v):
  //   255*0,1
endmodule

/* Code that sets the parameters or builds the circuit:
data := [];
*/
