// Digital circuit SP.dig as structural Verilog
// stack pointer
module SP (
  input  INC,
  input  DEC,
  input  C,
  input  D_RE,
  input  D_WE,
  input  A_RE,
  input  A_WE,
  input  [15:0] D_A,
  input  [7:0] D_D,
  output [7:0] Q
);

  wire and_1_out, and_2_out, and_3_out, edge_pulse_detector_1_plus, or_1_out, xor_1_out;
  wire [7:0] driver_1_out, not_2_out, var_adder_1_out_4;
  wire [15:8] driver_1_out_2;

  or or_1 (or_1_out, DEC, INC, xor_1_out);
  and and_1 (and_1_out, or_1_out, edge_pulse_detector_1_plus);
  edge_pulse_detector edge_pulse_detector_1 (.clk(C), .plus(edge_pulse_detector_1_plus));
  and and_2 (and_2_out, ~D_WE, A_WE);  // And
  assign {driver_1_out_2, driver_1_out} = and_2_out ? D_A : 16'bz;  // Driver driver_1
  // var_DFF_with_init #(.generic("bits := 8; init := 0xff;")) var_dff_with_init_1: pin names not known; wires that end beside it: driver_1_out, and_1_out, Q, D_A, D_D
  xor xor_1 (xor_1_out, A_WE, D_WE);
  assign D_A = A_RE ? {8'h1, Q} : 16'bz;  // Driver driver_2
  var_adder #(.generic("bits := 8;")) var_adder_1 (.A(Q), .c_i(1'b1), .out_4(var_adder_1_out_4));  // open: B, c_o
  // var_adder #(.generic("bits := 8;")) var_adder_2: pin names not known; wires that end beside it: 1'b1
  // Not not_1 has open pins: in=Q, out=open
  assign D_D = D_RE ? Q : 8'bz;  // Driver driver_3
  // Not not_2 has open pins: in=open, out=not_2_out
  and and_3 (and_3_out, D_WE, ~A_WE);  // And
  assign driver_1_out = and_3_out ? D_D : 8'bz;  // Driver driver_4
  assign driver_1_out = INC ? var_adder_1_out_4 : 8'bz;  // Driver driver_5
  assign driver_1_out = DEC ? not_2_out : 8'bz;  // Driver driver_6

  // Notes on the sheet:
  //   INC: increment
  //   DEC: decrement
endmodule
