// Digital circuit address control.dig as structural Verilog
// address control
module address_control (
  input  [7:0] X,
  input  [7:0] Y,
  input  [15:0] A,
  input  [3:0] M,
  output [15:0] O
);

  wire var_adder_3_p2, var_adder_4_p2;
  wire [7:0] var_adder_1_p2, var_adder_2_p2, var_adder_5_p3, var_adder_6_p2;

  // var_adder #(.generic("bits := 8;")) var_adder_1: pin names not known; wires that end beside it: X, var_adder_1_p2
  // var_adder #(.generic("bits := 8;")) var_adder_2: pin names not known; wires that end beside it: Y, var_adder_2_p2
  // var_adder #(.generic("bits := 16;")) var_adder_3: pin names not known; wires that end beside it: A, var_adder_3_p2
  // var_adder #(.generic("bits := 16;")) var_adder_4: pin names not known; wires that end beside it: A, var_adder_4_p2
  // var_adder #(.generic("bits := 8;")) var_adder_5: pin names not known; wires that end beside it: X, 1'b1, var_adder_5_p3
  // var_adder #(.generic("bits := 8;")) var_adder_6: pin names not known; wires that end beside it: 1'b1, var_adder_6_p2
  // var_multiplexer #(.generic("data_bits := 16; sel_bits := 4; sel_pos := \"top\";")) var_multiplexer_1: pin names not known; wires that end beside it: M, A, {{8{1'b0}}, var_adder_1_p2}, {{8{1'b0}}, var_adder_2_p2}, var_adder_3_p2, var_adder_4_p2, {{8{1'b0}}, var_adder_5_p3}, {{8{1'b0}}, var_adder_6_p2}, {{8{1'b0}}, A[7:0]}, A, A, A, A, A, A, A, A, O

  // Notes on the sheet:
  //   X: X register
  //   Y: Y register
  //   A: address in
  //   M: mode
  //   O: address out
  //   M: addressing modes
  //   000 - no change
  //   001 - zero page x
  //   010 - zero page y
  //   101 - absolute x
  //   110 - absolute y
endmodule
