// Digital circuit +edge pulse detector.dig as structural Verilog
module edge_pulse_detector (
  input  clk,
  output plus
);

  wire delay_1_out;

  and and_1 (plus, clk, delay_1_out);
  Delay #(.delayTime(2)) delay_1 (.out(delay_1_out));  // open: in
endmodule
