// Digital circuit kb diode relay ver.dig as structural Verilog
module kb_diode_relay_ver (
  input  clk,
  input  WE,
  input  [7:0] D,
  output [6:0] key
);

  wire _0_out, _1_out, _2_out, _3_out, _4_out, _5_out, _6_out, _7_out, _8_out, _9_out, A_out, B_out,
       BACK_QUOTE_out, BACK_SLASH_out, C_out, CLOSE_BRACKET_out, COMMA_out, D_out, diodeforward_1_out, E_out,
       EQUALS_out, F_out, G_out, H_out, I_out, J_out, K_out, L_out, M_out, MINUS_out, N_out, O_out,
       OPEN_BRACKET_out, or_1_out, P_out, PERIOD_out, Q_out, QUOTE_out, R_out, relaydt_1_p1, relaydt_1_p3,
       relaydt_1_p4, relaydt_1_p5, relaydt_1_p6, relaydt_1_p7, relaydt_1_p8, relaydt_1_p9, relaydt_1_p10,
       relaydt_1_p11, relaydt_1_p12, relaydt_1_p13, relaydt_1_p14, relaydt_1_p15, relaydt_1_p16,
       relaydt_1_p17, relaydt_1_p18, relaydt_1_p19, relaydt_1_p20, relaydt_1_p21, relaydt_1_p22,
       relaydt_1_p23, relaydt_1_p24, relaydt_1_p25, relaydt_1_p26, relaydt_1_p27, relaydt_1_p28,
       relaydt_1_p29, relaydt_1_p30, relaydt_1_p31, relaydt_2_p1, relaydt_2_p2, relaydt_2_p3, relaydt_2_p4,
       relaydt_2_p5, relaydt_2_p6, relaydt_2_p7, relaydt_2_p8, relaydt_2_p9, relaydt_2_p10, relaydt_2_p11,
       relaydt_2_p12, relaydt_2_p13, relaydt_2_p14, relaydt_2_p15, relaydt_2_p16, relaydt_2_p18,
       relaydt_2_p19, relaydt_2_p20, relaydt_2_p21, relaydt_2_p22, relaydt_2_p23, relaydt_2_p24,
       relaydt_2_p25, relaydt_2_p26, relaydt_2_p27, relaydt_2_p28, relaydt_2_p29, relaydt_2_p30,
       relaydt_2_p31, relaydt_2_p32, relaydt_2_p33, relaydt_2_p34, relaydt_2_p35, relaydt_2_p36,
       relaydt_2_p37, relaydt_2_p38, relaydt_2_p39, relaydt_2_p40, relaydt_2_p41, relaydt_2_p42,
       relaydt_2_p43, relaydt_2_p44, S_out, SEMICOLON_out, SLASH_out, T_out, U_out, undriven, undriven_2,
       undriven_3, undriven_4, undriven_5, undriven_6, undriven_7, V_out, var_dff_with_init_1_p2,
       var_dff_with_init_1_p3, var_dff_with_init_1_p4, var_dff_with_init_1_p5, var_dff_with_init_1_p6,
       var_dff_with_init_1_p7, var_dff_with_init_1_p8, var_dff_with_init_1_p9, var_dff_with_init_1_p10,
       var_dff_with_init_1_p11, var_dff_with_init_1_p12, var_dff_with_init_1_p13, var_dff_with_init_1_p14,
       var_dff_with_init_1_p15, var_dff_with_init_1_p16, W_out, X_out, Y_out, Z_out;
  wire [6:0] diodeforward_361_out, driver_1_out;

  DiodeForward diodeforward_1 (.in(A_out), .out(diodeforward_1_out));
  DiodeForward diodeforward_2 (.in(B_out), .out(diodeforward_1_out));
  DiodeForward diodeforward_3 (.in(C_out), .out(diodeforward_1_out));
  DiodeForward diodeforward_4 (.in(D_out), .out(diodeforward_1_out));
  DiodeForward diodeforward_5 (.in(E_out), .out(diodeforward_1_out));
  DiodeForward diodeforward_6 (.in(F_out), .out(diodeforward_1_out));
  DiodeForward diodeforward_7 (.in(G_out), .out(diodeforward_1_out));
  DiodeForward diodeforward_8 (.in(H_out), .out(diodeforward_1_out));
  DiodeForward diodeforward_9 (.in(I_out), .out(diodeforward_1_out));
  DiodeForward diodeforward_10 (.in(J_out), .out(diodeforward_1_out));
  DiodeForward diodeforward_11 (.in(K_out), .out(diodeforward_1_out));
  DiodeForward diodeforward_12 (.in(L_out), .out(diodeforward_1_out));
  DiodeForward diodeforward_13 (.in(M_out), .out(diodeforward_1_out));
  DiodeForward diodeforward_14 (.in(N_out), .out(diodeforward_1_out));
  DiodeForward diodeforward_15 (.in(O_out), .out(diodeforward_1_out));
  DiodeForward diodeforward_16 (.in(P_out), .out(diodeforward_1_out));
  DiodeForward diodeforward_17 (.in(Q_out), .out(diodeforward_1_out));
  DiodeForward diodeforward_18 (.in(R_out), .out(diodeforward_1_out));
  DiodeForward diodeforward_19 (.in(S_out), .out(diodeforward_1_out));
  DiodeForward diodeforward_20 (.in(T_out), .out(diodeforward_1_out));
  DiodeForward diodeforward_21 (.in(U_out), .out(diodeforward_1_out));
  DiodeForward diodeforward_22 (.in(V_out), .out(diodeforward_1_out));
  DiodeForward diodeforward_23 (.in(W_out), .out(diodeforward_1_out));
  DiodeForward diodeforward_24 (.in(X_out), .out(diodeforward_1_out));
  DiodeForward diodeforward_25 (.in(Y_out), .out(diodeforward_1_out));
  DiodeForward diodeforward_26 (.in(Z_out), .out(diodeforward_1_out));
  DiodeForward diodeforward_27 (.in(_1_out), .out(diodeforward_1_out));
  DiodeForward diodeforward_28 (.in(_2_out), .out(diodeforward_1_out));
  DiodeForward diodeforward_29 (.in(_3_out), .out(diodeforward_1_out));
  DiodeForward diodeforward_30 (.in(_4_out), .out(diodeforward_1_out));
  DiodeForward diodeforward_31 (.in(_5_out), .out(diodeforward_1_out));
  DiodeForward diodeforward_32 (.in(_6_out), .out(diodeforward_1_out));
  DiodeForward diodeforward_33 (.in(_7_out), .out(diodeforward_1_out));
  DiodeForward diodeforward_34 (.in(_8_out), .out(diodeforward_1_out));
  DiodeForward diodeforward_35 (.in(_9_out), .out(diodeforward_1_out));
  DiodeForward diodeforward_36 (.in(_0_out), .out(diodeforward_1_out));
  DiodeForward diodeforward_37 (.in(BACK_QUOTE_out), .out(diodeforward_1_out));
  DiodeForward diodeforward_38 (.in(MINUS_out), .out(diodeforward_1_out));
  DiodeForward diodeforward_39 (.in(EQUALS_out), .out(diodeforward_1_out));
  DiodeForward diodeforward_40 (.in(OPEN_BRACKET_out), .out(diodeforward_1_out));
  DiodeForward diodeforward_41 (.in(CLOSE_BRACKET_out), .out(diodeforward_1_out));
  DiodeForward diodeforward_42 (.in(BACK_SLASH_out), .out(diodeforward_1_out));
  DiodeForward diodeforward_43 (.in(SEMICOLON_out), .out(diodeforward_1_out));
  DiodeForward diodeforward_44 (.in(QUOTE_out), .out(diodeforward_1_out));
  DiodeForward diodeforward_45 (.in(COMMA_out), .out(diodeforward_1_out));
  DiodeForward diodeforward_46 (.in(PERIOD_out), .out(diodeforward_1_out));
  DiodeForward diodeforward_47 (.in(SLASH_out), .out(diodeforward_1_out));
  PullDown pulldown_1 (.out(diodeforward_1_out));
  or or_1 (or_1_out, diodeforward_1_out, WE);
  assign driver_1_out = WE ? D[6:0] : 7'bz;  // Driver driver_1
  Button A (.out(A_out));
  // RelayDT #(.poles(26)) relaydt_1: pin names not known; wires that end beside it: relaydt_1_p1, 1'b0, relaydt_1_p3, relaydt_1_p4, relaydt_1_p5, relaydt_1_p6, relaydt_1_p7, relaydt_1_p8, relaydt_1_p9, relaydt_1_p10, relaydt_1_p11, relaydt_1_p12, relaydt_1_p13, relaydt_1_p14, relaydt_1_p15, relaydt_1_p16, relaydt_1_p17, relaydt_1_p18, relaydt_1_p19, relaydt_1_p20, relaydt_1_p21, relaydt_1_p22, relaydt_1_p23, relaydt_1_p24, relaydt_1_p25, relaydt_1_p26, relaydt_1_p27, relaydt_1_p28, relaydt_1_p29, relaydt_1_p30, relaydt_1_p31
  Button B (.out(B_out));
  Button C (.out(C_out));
  Button u_D (.out(D_out));
  Button E (.out(E_out));
  Button F (.out(F_out));
  Button G (.out(G_out));
  Button H (.out(H_out));
  Button I (.out(I_out));
  Button J (.out(J_out));
  Button K (.out(K_out));
  Button L (.out(L_out));
  Button M (.out(M_out));
  Button N (.out(N_out));
  Button O (.out(O_out));
  Button P (.out(P_out));
  Button Q (.out(Q_out));
  Button R (.out(R_out));
  Button S (.out(S_out));
  Button T (.out(T_out));
  Button U (.out(U_out));
  Button V (.out(V_out));
  Button W (.out(W_out));
  Button X (.out(X_out));
  Button Y (.out(Y_out));
  Button Z (.out(Z_out));
  Button SHIFT (.out(relaydt_1_p1));
  Button _1 (.out(_1_out));
  // RelayDT #(.poles(21)) relaydt_2: pin names not known; wires that end beside it: relaydt_2_p1, relaydt_2_p2, relaydt_2_p3, relaydt_2_p4, relaydt_2_p5, relaydt_2_p6, relaydt_2_p7, relaydt_2_p8, relaydt_2_p9, relaydt_2_p10, relaydt_2_p11, relaydt_2_p12, relaydt_2_p13, relaydt_2_p14, relaydt_2_p15, relaydt_2_p16, 1'b0, relaydt_2_p18, relaydt_2_p19, relaydt_2_p20, relaydt_2_p21, relaydt_2_p22, relaydt_2_p23, relaydt_2_p24, relaydt_2_p25, relaydt_2_p26, relaydt_2_p27, relaydt_2_p28, relaydt_2_p29, relaydt_2_p30, relaydt_2_p31, relaydt_2_p32, relaydt_2_p33, relaydt_2_p34, relaydt_2_p35, relaydt_2_p36, relaydt_2_p37, relaydt_2_p38, relaydt_2_p39, relaydt_2_p40, relaydt_2_p41, relaydt_2_p42, relaydt_2_p43, relaydt_2_p44
  Button _2 (.out(_2_out));
  Button _3 (.out(_3_out));
  Button _4 (.out(_4_out));
  Button _5 (.out(_5_out));
  Button _6 (.out(_6_out));
  Button _7 (.out(_7_out));
  Button _8 (.out(_8_out));
  Button _9 (.out(_9_out));
  Button _0 (.out(_0_out));
  Button BACK_QUOTE (.out(BACK_QUOTE_out));
  Button MINUS (.out(MINUS_out));
  Button EQUALS (.out(EQUALS_out));
  Button OPEN_BRACKET (.out(OPEN_BRACKET_out));
  Button CLOSE_BRACKET (.out(CLOSE_BRACKET_out));
  Button BACK_SLASH (.out(BACK_SLASH_out));
  Button SEMICOLON (.out(SEMICOLON_out));
  Button QUOTE (.out(QUOTE_out));
  Button COMMA (.out(COMMA_out));
  Button PERIOD (.out(PERIOD_out));
  Button SLASH (.out(SLASH_out));
  // var_DFF_with_init #(.generic("bits := 7; init := 0;")) var_dff_with_init_1: pin names not known; wires that end beside it: driver_1_out, var_dff_with_init_1_p2, var_dff_with_init_1_p3, var_dff_with_init_1_p4, var_dff_with_init_1_p5, var_dff_with_init_1_p6, var_dff_with_init_1_p7, var_dff_with_init_1_p8, var_dff_with_init_1_p9, var_dff_with_init_1_p10, var_dff_with_init_1_p11, var_dff_with_init_1_p12, var_dff_with_init_1_p13, var_dff_with_init_1_p14, var_dff_with_init_1_p15, var_dff_with_init_1_p16, key
  // And and_1 has open pins: In_1=or_1_out, In_2=clk, out=open
  assign driver_1_out = ~WE ? diodeforward_361_out : 7'bz;  // DriverInvSel driverinvsel_1
  DiodeForward diodeforward_48 (.in(relaydt_2_p38), .out(diodeforward_361_out[6]));
  PullDown pulldown_2 (.out(diodeforward_361_out[6]));
  DiodeForward diodeforward_49 (.in(relaydt_2_p16), .out(diodeforward_361_out[6]));
  DiodeForward diodeforward_50 (.in(relaydt_2_p44), .out(diodeforward_361_out[6]));
  DiodeForward diodeforward_51 (.in(var_dff_with_init_1_p5), .out(diodeforward_361_out[6]));
  DiodeForward diodeforward_52 (.in(var_dff_with_init_1_p3), .out(diodeforward_361_out[6]));
  DiodeForward diodeforward_53 (.in(relaydt_2_p8), .out(diodeforward_361_out[6]));
  DiodeForward diodeforward_54 (.in(relaydt_2_p10), .out(diodeforward_361_out[6]));
  DiodeForward diodeforward_55 (.in(relaydt_2_p12), .out(diodeforward_361_out[6]));
  DiodeForward diodeforward_56 (.in(relaydt_2_p14), .out(diodeforward_361_out[6]));
  DiodeForward diodeforward_57 (.in(undriven), .out(diodeforward_361_out[6]));
  DiodeForward diodeforward_58 (.in(relaydt_2_p2), .out(diodeforward_361_out[6]));
  DiodeForward diodeforward_59 (.in(relaydt_2_p4), .out(diodeforward_361_out[6]));
  DiodeForward diodeforward_60 (.in(relaydt_2_p6), .out(diodeforward_361_out[6]));
  DiodeForward diodeforward_61 (.in(relaydt_1_p30), .out(diodeforward_361_out[6]));
  DiodeForward diodeforward_62 (.in(undriven_7), .out(diodeforward_361_out[6]));
  DiodeForward diodeforward_63 (.in(undriven_5), .out(diodeforward_361_out[6]));
  DiodeForward diodeforward_64 (.in(undriven_3), .out(diodeforward_361_out[6]));
  DiodeForward diodeforward_65 (.in(relaydt_1_p22), .out(diodeforward_361_out[6]));
  DiodeForward diodeforward_66 (.in(relaydt_1_p24), .out(diodeforward_361_out[6]));
  DiodeForward diodeforward_67 (.in(relaydt_1_p26), .out(diodeforward_361_out[6]));
  DiodeForward diodeforward_68 (.in(relaydt_1_p28), .out(diodeforward_361_out[6]));
  DiodeForward diodeforward_69 (.in(relaydt_1_p14), .out(diodeforward_361_out[6]));
  DiodeForward diodeforward_70 (.in(relaydt_1_p16), .out(diodeforward_361_out[6]));
  DiodeForward diodeforward_71 (.in(relaydt_1_p18), .out(diodeforward_361_out[6]));
  DiodeForward diodeforward_72 (.in(relaydt_1_p20), .out(diodeforward_361_out[6]));
  DiodeForward diodeforward_73 (.in(relaydt_1_p6), .out(diodeforward_361_out[6]));
  DiodeForward diodeforward_74 (.in(relaydt_1_p8), .out(diodeforward_361_out[6]));
  DiodeForward diodeforward_75 (.in(relaydt_1_p10), .out(diodeforward_361_out[6]));
  DiodeForward diodeforward_76 (.in(relaydt_1_p12), .out(diodeforward_361_out[6]));
  DiodeForward diodeforward_77 (.in(relaydt_2_p28), .out(diodeforward_361_out[6]));
  DiodeForward diodeforward_78 (.in(relaydt_2_p40), .out(diodeforward_361_out[6]));
  DiodeForward diodeforward_79 (.in(relaydt_2_p39), .out(diodeforward_361_out[6]));
  DiodeForward diodeforward_80 (.in(relaydt_1_p4), .out(diodeforward_361_out[6]));
  DiodeForward diodeforward_81 (.in(relaydt_2_p15), .out(diodeforward_361_out[6]));
  DiodeForward diodeforward_82 (.in(var_dff_with_init_1_p2), .out(diodeforward_361_out[6]));
  DiodeForward diodeforward_83 (.in(var_dff_with_init_1_p6), .out(diodeforward_361_out[6]));
  DiodeForward diodeforward_84 (.in(var_dff_with_init_1_p4), .out(diodeforward_361_out[6]));
  DiodeForward diodeforward_85 (.in(relaydt_2_p7), .out(diodeforward_361_out[6]));
  DiodeForward diodeforward_86 (.in(relaydt_2_p9), .out(diodeforward_361_out[6]));
  DiodeForward diodeforward_87 (.in(relaydt_2_p11), .out(diodeforward_361_out[6]));
  DiodeForward diodeforward_88 (.in(relaydt_2_p13), .out(diodeforward_361_out[6]));
  DiodeForward diodeforward_89 (.in(undriven_2), .out(diodeforward_361_out[6]));
  DiodeForward diodeforward_90 (.in(relaydt_2_p1), .out(diodeforward_361_out[6]));
  DiodeForward diodeforward_91 (.in(relaydt_2_p3), .out(diodeforward_361_out[6]));
  DiodeForward diodeforward_92 (.in(relaydt_2_p5), .out(diodeforward_361_out[6]));
  DiodeForward diodeforward_93 (.in(relaydt_1_p29), .out(diodeforward_361_out[6]));
  DiodeForward diodeforward_94 (.in(relaydt_1_p31), .out(diodeforward_361_out[6]));
  DiodeForward diodeforward_95 (.in(undriven_6), .out(diodeforward_361_out[6]));
  DiodeForward diodeforward_96 (.in(undriven_4), .out(diodeforward_361_out[6]));
  DiodeForward diodeforward_97 (.in(relaydt_1_p21), .out(diodeforward_361_out[6]));
  DiodeForward diodeforward_98 (.in(relaydt_1_p23), .out(diodeforward_361_out[6]));
  DiodeForward diodeforward_99 (.in(relaydt_1_p25), .out(diodeforward_361_out[6]));
  DiodeForward diodeforward_100 (.in(relaydt_1_p27), .out(diodeforward_361_out[6]));
  DiodeForward diodeforward_101 (.in(relaydt_1_p13), .out(diodeforward_361_out[6]));
  DiodeForward diodeforward_102 (.in(relaydt_1_p15), .out(diodeforward_361_out[6]));
  DiodeForward diodeforward_103 (.in(relaydt_1_p17), .out(diodeforward_361_out[6]));
  DiodeForward diodeforward_104 (.in(relaydt_1_p19), .out(diodeforward_361_out[6]));
  DiodeForward diodeforward_105 (.in(relaydt_1_p5), .out(diodeforward_361_out[6]));
  DiodeForward diodeforward_106 (.in(relaydt_1_p7), .out(diodeforward_361_out[6]));
  DiodeForward diodeforward_107 (.in(relaydt_1_p9), .out(diodeforward_361_out[6]));
  DiodeForward diodeforward_108 (.in(relaydt_1_p11), .out(diodeforward_361_out[6]));
  DiodeForward diodeforward_109 (.in(relaydt_2_p20), .out(diodeforward_361_out[6]));
  DiodeForward diodeforward_110 (.in(relaydt_1_p3), .out(diodeforward_361_out[6]));
  DiodeForward diodeforward_111 (.in(relaydt_2_p38), .out(diodeforward_361_out[5]));
  PullDown pulldown_3 (.out(diodeforward_361_out[5]));
  DiodeForward diodeforward_112 (.in(relaydt_2_p16), .out(diodeforward_361_out[5]));
  DiodeForward diodeforward_113 (.in(relaydt_2_p44), .out(diodeforward_361_out[5]));
  DiodeForward diodeforward_114 (.in(var_dff_with_init_1_p5), .out(diodeforward_361_out[5]));
  DiodeForward diodeforward_115 (.in(var_dff_with_init_1_p3), .out(diodeforward_361_out[5]));
  DiodeForward diodeforward_116 (.in(relaydt_2_p8), .out(diodeforward_361_out[5]));
  DiodeForward diodeforward_117 (.in(relaydt_2_p10), .out(diodeforward_361_out[5]));
  DiodeForward diodeforward_118 (.in(relaydt_2_p12), .out(diodeforward_361_out[5]));
  DiodeForward diodeforward_119 (.in(relaydt_2_p14), .out(diodeforward_361_out[5]));
  DiodeForward diodeforward_120 (.in(undriven), .out(diodeforward_361_out[5]));
  DiodeForward diodeforward_121 (.in(relaydt_2_p2), .out(diodeforward_361_out[5]));
  DiodeForward diodeforward_122 (.in(relaydt_2_p4), .out(diodeforward_361_out[5]));
  DiodeForward diodeforward_123 (.in(relaydt_2_p6), .out(diodeforward_361_out[5]));
  DiodeForward diodeforward_124 (.in(relaydt_1_p30), .out(diodeforward_361_out[5]));
  DiodeForward diodeforward_125 (.in(undriven_7), .out(diodeforward_361_out[5]));
  DiodeForward diodeforward_126 (.in(undriven_5), .out(diodeforward_361_out[5]));
  DiodeForward diodeforward_127 (.in(undriven_3), .out(diodeforward_361_out[5]));
  DiodeForward diodeforward_128 (.in(relaydt_1_p22), .out(diodeforward_361_out[5]));
  DiodeForward diodeforward_129 (.in(relaydt_1_p24), .out(diodeforward_361_out[5]));
  DiodeForward diodeforward_130 (.in(relaydt_1_p26), .out(diodeforward_361_out[5]));
  DiodeForward diodeforward_131 (.in(relaydt_1_p28), .out(diodeforward_361_out[5]));
  DiodeForward diodeforward_132 (.in(relaydt_1_p14), .out(diodeforward_361_out[5]));
  DiodeForward diodeforward_133 (.in(relaydt_1_p16), .out(diodeforward_361_out[5]));
  DiodeForward diodeforward_134 (.in(relaydt_1_p18), .out(diodeforward_361_out[5]));
  DiodeForward diodeforward_135 (.in(relaydt_1_p20), .out(diodeforward_361_out[5]));
  DiodeForward diodeforward_136 (.in(relaydt_1_p6), .out(diodeforward_361_out[5]));
  DiodeForward diodeforward_137 (.in(relaydt_1_p8), .out(diodeforward_361_out[5]));
  DiodeForward diodeforward_138 (.in(relaydt_1_p10), .out(diodeforward_361_out[5]));
  DiodeForward diodeforward_139 (.in(relaydt_1_p12), .out(diodeforward_361_out[5]));
  DiodeForward diodeforward_140 (.in(var_dff_with_init_1_p13), .out(diodeforward_361_out[5]));
  DiodeForward diodeforward_141 (.in(var_dff_with_init_1_p15), .out(diodeforward_361_out[5]));
  DiodeForward diodeforward_142 (.in(relaydt_2_p39), .out(diodeforward_361_out[5]));
  DiodeForward diodeforward_143 (.in(relaydt_1_p4), .out(diodeforward_361_out[5]));
  DiodeForward diodeforward_144 (.in(var_dff_with_init_1_p7), .out(diodeforward_361_out[5]));
  DiodeForward diodeforward_145 (.in(var_dff_with_init_1_p8), .out(diodeforward_361_out[5]));
  DiodeForward diodeforward_146 (.in(var_dff_with_init_1_p11), .out(diodeforward_361_out[5]));
  DiodeForward diodeforward_147 (.in(relaydt_2_p43), .out(diodeforward_361_out[5]));
  DiodeForward diodeforward_148 (.in(relaydt_2_p31), .out(diodeforward_361_out[5]));
  DiodeForward diodeforward_149 (.in(relaydt_2_p33), .out(diodeforward_361_out[5]));
  DiodeForward diodeforward_150 (.in(relaydt_2_p35), .out(diodeforward_361_out[5]));
  DiodeForward diodeforward_151 (.in(relaydt_2_p37), .out(diodeforward_361_out[5]));
  DiodeForward diodeforward_152 (.in(relaydt_2_p23), .out(diodeforward_361_out[5]));
  DiodeForward diodeforward_153 (.in(relaydt_2_p25), .out(diodeforward_361_out[5]));
  DiodeForward diodeforward_154 (.in(relaydt_2_p27), .out(diodeforward_361_out[5]));
  DiodeForward diodeforward_155 (.in(relaydt_2_p29), .out(diodeforward_361_out[5]));
  DiodeForward diodeforward_156 (.in(var_dff_with_init_1_p14), .out(diodeforward_361_out[5]));
  DiodeForward diodeforward_157 (.in(var_dff_with_init_1_p16), .out(diodeforward_361_out[5]));
  DiodeForward diodeforward_158 (.in(relaydt_2_p19), .out(diodeforward_361_out[5]));
  DiodeForward diodeforward_159 (.in(relaydt_2_p21), .out(diodeforward_361_out[5]));
  DiodeForward diodeforward_160 (.in(relaydt_2_p32), .out(diodeforward_361_out[5]));
  DiodeForward diodeforward_161 (.in(relaydt_2_p42), .out(diodeforward_361_out[5]));
  DiodeForward diodeforward_162 (.in(var_dff_with_init_1_p12), .out(diodeforward_361_out[5]));
  DiodeForward diodeforward_163 (.in(relaydt_2_p41), .out(diodeforward_361_out[5]));
  DiodeForward diodeforward_164 (.in(relaydt_2_p30), .out(diodeforward_361_out[5]));
  DiodeForward diodeforward_165 (.in(var_dff_with_init_1_p10), .out(diodeforward_361_out[5]));
  DiodeForward diodeforward_166 (.in(relaydt_2_p34), .out(diodeforward_361_out[5]));
  DiodeForward diodeforward_167 (.in(relaydt_2_p36), .out(diodeforward_361_out[5]));
  DiodeForward diodeforward_168 (.in(var_dff_with_init_1_p9), .out(diodeforward_361_out[5]));
  DiodeForward diodeforward_169 (.in(relaydt_2_p22), .out(diodeforward_361_out[5]));
  DiodeForward diodeforward_170 (.in(relaydt_2_p24), .out(diodeforward_361_out[5]));
  DiodeForward diodeforward_171 (.in(relaydt_2_p26), .out(diodeforward_361_out[5]));
  DiodeForward diodeforward_172 (.in(relaydt_2_p18), .out(diodeforward_361_out[5]));
  DiodeForward diodeforward_173 (.in(var_dff_with_init_1_p3), .out(diodeforward_361_out[4]));
  DiodeForward diodeforward_174 (.in(relaydt_2_p38), .out(diodeforward_361_out[4]));
  PullDown pulldown_4 (.out(diodeforward_361_out[4]));
  DiodeForward diodeforward_175 (.in(relaydt_2_p14), .out(diodeforward_361_out[4]));
  DiodeForward diodeforward_176 (.in(relaydt_2_p16), .out(diodeforward_361_out[4]));
  DiodeForward diodeforward_177 (.in(relaydt_2_p44), .out(diodeforward_361_out[4]));
  DiodeForward diodeforward_178 (.in(var_dff_with_init_1_p5), .out(diodeforward_361_out[4]));
  DiodeForward diodeforward_179 (.in(relaydt_2_p6), .out(diodeforward_361_out[4]));
  DiodeForward diodeforward_180 (.in(relaydt_2_p8), .out(diodeforward_361_out[4]));
  DiodeForward diodeforward_181 (.in(relaydt_2_p10), .out(diodeforward_361_out[4]));
  DiodeForward diodeforward_182 (.in(relaydt_2_p12), .out(diodeforward_361_out[4]));
  DiodeForward diodeforward_183 (.in(undriven_3), .out(diodeforward_361_out[4]));
  DiodeForward diodeforward_184 (.in(undriven), .out(diodeforward_361_out[4]));
  DiodeForward diodeforward_185 (.in(relaydt_2_p2), .out(diodeforward_361_out[4]));
  DiodeForward diodeforward_186 (.in(relaydt_2_p4), .out(diodeforward_361_out[4]));
  DiodeForward diodeforward_187 (.in(var_dff_with_init_1_p4), .out(diodeforward_361_out[4]));
  DiodeForward diodeforward_188 (.in(relaydt_2_p28), .out(diodeforward_361_out[4]));
  DiodeForward diodeforward_189 (.in(relaydt_2_p40), .out(diodeforward_361_out[4]));
  DiodeForward diodeforward_190 (.in(undriven_5), .out(diodeforward_361_out[4]));
  DiodeForward diodeforward_191 (.in(relaydt_2_p13), .out(diodeforward_361_out[4]));
  DiodeForward diodeforward_192 (.in(relaydt_2_p15), .out(diodeforward_361_out[4]));
  DiodeForward diodeforward_193 (.in(var_dff_with_init_1_p2), .out(diodeforward_361_out[4]));
  DiodeForward diodeforward_194 (.in(var_dff_with_init_1_p6), .out(diodeforward_361_out[4]));
  DiodeForward diodeforward_195 (.in(relaydt_2_p5), .out(diodeforward_361_out[4]));
  DiodeForward diodeforward_196 (.in(relaydt_2_p7), .out(diodeforward_361_out[4]));
  DiodeForward diodeforward_197 (.in(relaydt_2_p9), .out(diodeforward_361_out[4]));
  DiodeForward diodeforward_198 (.in(relaydt_2_p11), .out(diodeforward_361_out[4]));
  DiodeForward diodeforward_199 (.in(undriven_4), .out(diodeforward_361_out[4]));
  DiodeForward diodeforward_200 (.in(undriven_2), .out(diodeforward_361_out[4]));
  DiodeForward diodeforward_201 (.in(relaydt_2_p1), .out(diodeforward_361_out[4]));
  DiodeForward diodeforward_202 (.in(relaydt_2_p3), .out(diodeforward_361_out[4]));
  DiodeForward diodeforward_203 (.in(relaydt_2_p43), .out(diodeforward_361_out[4]));
  DiodeForward diodeforward_204 (.in(var_dff_with_init_1_p13), .out(diodeforward_361_out[4]));
  DiodeForward diodeforward_205 (.in(var_dff_with_init_1_p15), .out(diodeforward_361_out[4]));
  DiodeForward diodeforward_206 (.in(undriven_6), .out(diodeforward_361_out[4]));
  DiodeForward diodeforward_207 (.in(relaydt_2_p37), .out(diodeforward_361_out[4]));
  DiodeForward diodeforward_208 (.in(var_dff_with_init_1_p7), .out(diodeforward_361_out[4]));
  DiodeForward diodeforward_209 (.in(var_dff_with_init_1_p8), .out(diodeforward_361_out[4]));
  DiodeForward diodeforward_210 (.in(var_dff_with_init_1_p11), .out(diodeforward_361_out[4]));
  DiodeForward diodeforward_211 (.in(relaydt_2_p29), .out(diodeforward_361_out[4]));
  DiodeForward diodeforward_212 (.in(relaydt_2_p31), .out(diodeforward_361_out[4]));
  DiodeForward diodeforward_213 (.in(relaydt_2_p33), .out(diodeforward_361_out[4]));
  DiodeForward diodeforward_214 (.in(relaydt_2_p35), .out(diodeforward_361_out[4]));
  DiodeForward diodeforward_215 (.in(relaydt_2_p21), .out(diodeforward_361_out[4]));
  DiodeForward diodeforward_216 (.in(relaydt_2_p23), .out(diodeforward_361_out[4]));
  DiodeForward diodeforward_217 (.in(relaydt_2_p25), .out(diodeforward_361_out[4]));
  DiodeForward diodeforward_218 (.in(relaydt_2_p27), .out(diodeforward_361_out[4]));
  DiodeForward diodeforward_219 (.in(relaydt_2_p19), .out(diodeforward_361_out[4]));
  DiodeForward diodeforward_220 (.in(var_dff_with_init_1_p3), .out(diodeforward_361_out[3]));
  DiodeForward diodeforward_221 (.in(relaydt_2_p38), .out(diodeforward_361_out[3]));
  PullDown pulldown_5 (.out(diodeforward_361_out[3]));
  DiodeForward diodeforward_222 (.in(relaydt_2_p14), .out(diodeforward_361_out[3]));
  DiodeForward diodeforward_223 (.in(relaydt_2_p16), .out(diodeforward_361_out[3]));
  DiodeForward diodeforward_224 (.in(relaydt_2_p44), .out(diodeforward_361_out[3]));
  DiodeForward diodeforward_225 (.in(var_dff_with_init_1_p5), .out(diodeforward_361_out[3]));
  DiodeForward diodeforward_226 (.in(relaydt_1_p28), .out(diodeforward_361_out[3]));
  DiodeForward diodeforward_227 (.in(relaydt_1_p30), .out(diodeforward_361_out[3]));
  DiodeForward diodeforward_228 (.in(undriven_7), .out(diodeforward_361_out[3]));
  DiodeForward diodeforward_229 (.in(relaydt_2_p12), .out(diodeforward_361_out[3]));
  DiodeForward diodeforward_230 (.in(relaydt_1_p20), .out(diodeforward_361_out[3]));
  DiodeForward diodeforward_231 (.in(relaydt_1_p22), .out(diodeforward_361_out[3]));
  DiodeForward diodeforward_232 (.in(relaydt_1_p24), .out(diodeforward_361_out[3]));
  DiodeForward diodeforward_233 (.in(relaydt_1_p26), .out(diodeforward_361_out[3]));
  DiodeForward diodeforward_234 (.in(var_dff_with_init_1_p4), .out(diodeforward_361_out[3]));
  DiodeForward diodeforward_235 (.in(relaydt_2_p28), .out(diodeforward_361_out[3]));
  DiodeForward diodeforward_236 (.in(relaydt_2_p40), .out(diodeforward_361_out[3]));
  DiodeForward diodeforward_237 (.in(relaydt_1_p18), .out(diodeforward_361_out[3]));
  DiodeForward diodeforward_238 (.in(relaydt_2_p13), .out(diodeforward_361_out[3]));
  DiodeForward diodeforward_239 (.in(relaydt_2_p15), .out(diodeforward_361_out[3]));
  DiodeForward diodeforward_240 (.in(var_dff_with_init_1_p2), .out(diodeforward_361_out[3]));
  DiodeForward diodeforward_241 (.in(var_dff_with_init_1_p6), .out(diodeforward_361_out[3]));
  DiodeForward diodeforward_242 (.in(relaydt_1_p27), .out(diodeforward_361_out[3]));
  DiodeForward diodeforward_243 (.in(relaydt_1_p29), .out(diodeforward_361_out[3]));
  DiodeForward diodeforward_244 (.in(relaydt_1_p31), .out(diodeforward_361_out[3]));
  DiodeForward diodeforward_245 (.in(relaydt_2_p11), .out(diodeforward_361_out[3]));
  DiodeForward diodeforward_246 (.in(relaydt_1_p19), .out(diodeforward_361_out[3]));
  DiodeForward diodeforward_247 (.in(relaydt_1_p21), .out(diodeforward_361_out[3]));
  DiodeForward diodeforward_248 (.in(relaydt_1_p23), .out(diodeforward_361_out[3]));
  DiodeForward diodeforward_249 (.in(relaydt_1_p25), .out(diodeforward_361_out[3]));
  DiodeForward diodeforward_250 (.in(relaydt_2_p43), .out(diodeforward_361_out[3]));
  DiodeForward diodeforward_251 (.in(var_dff_with_init_1_p13), .out(diodeforward_361_out[3]));
  DiodeForward diodeforward_252 (.in(var_dff_with_init_1_p15), .out(diodeforward_361_out[3]));
  DiodeForward diodeforward_253 (.in(relaydt_1_p17), .out(diodeforward_361_out[3]));
  DiodeForward diodeforward_254 (.in(relaydt_2_p37), .out(diodeforward_361_out[3]));
  DiodeForward diodeforward_255 (.in(var_dff_with_init_1_p7), .out(diodeforward_361_out[3]));
  DiodeForward diodeforward_256 (.in(var_dff_with_init_1_p8), .out(diodeforward_361_out[3]));
  DiodeForward diodeforward_257 (.in(var_dff_with_init_1_p11), .out(diodeforward_361_out[3]));
  DiodeForward diodeforward_258 (.in(relaydt_2_p41), .out(diodeforward_361_out[3]));
  DiodeForward diodeforward_259 (.in(var_dff_with_init_1_p14), .out(diodeforward_361_out[3]));
  DiodeForward diodeforward_260 (.in(var_dff_with_init_1_p16), .out(diodeforward_361_out[3]));
  DiodeForward diodeforward_261 (.in(relaydt_2_p35), .out(diodeforward_361_out[3]));
  DiodeForward diodeforward_262 (.in(relaydt_2_p36), .out(diodeforward_361_out[3]));
  DiodeForward diodeforward_263 (.in(relaydt_2_p32), .out(diodeforward_361_out[3]));
  DiodeForward diodeforward_264 (.in(relaydt_2_p42), .out(diodeforward_361_out[3]));
  DiodeForward diodeforward_265 (.in(var_dff_with_init_1_p12), .out(diodeforward_361_out[3]));
  DiodeForward diodeforward_266 (.in(relaydt_2_p34), .out(diodeforward_361_out[3]));
  DiodeForward diodeforward_267 (.in(var_dff_with_init_1_p3), .out(diodeforward_361_out[2]));
  DiodeForward diodeforward_268 (.in(relaydt_2_p38), .out(diodeforward_361_out[2]));
  PullDown pulldown_6 (.out(diodeforward_361_out[2]));
  DiodeForward diodeforward_269 (.in(relaydt_2_p6), .out(diodeforward_361_out[2]));
  DiodeForward diodeforward_270 (.in(relaydt_2_p8), .out(diodeforward_361_out[2]));
  DiodeForward diodeforward_271 (.in(relaydt_2_p10), .out(diodeforward_361_out[2]));
  DiodeForward diodeforward_272 (.in(var_dff_with_init_1_p5), .out(diodeforward_361_out[2]));
  DiodeForward diodeforward_273 (.in(relaydt_1_p28), .out(diodeforward_361_out[2]));
  DiodeForward diodeforward_274 (.in(relaydt_1_p30), .out(diodeforward_361_out[2]));
  DiodeForward diodeforward_275 (.in(undriven_7), .out(diodeforward_361_out[2]));
  DiodeForward diodeforward_276 (.in(relaydt_2_p4), .out(diodeforward_361_out[2]));
  DiodeForward diodeforward_277 (.in(relaydt_1_p12), .out(diodeforward_361_out[2]));
  DiodeForward diodeforward_278 (.in(relaydt_1_p14), .out(diodeforward_361_out[2]));
  DiodeForward diodeforward_279 (.in(relaydt_1_p16), .out(diodeforward_361_out[2]));
  DiodeForward diodeforward_280 (.in(relaydt_1_p26), .out(diodeforward_361_out[2]));
  DiodeForward diodeforward_281 (.in(var_dff_with_init_1_p4), .out(diodeforward_361_out[2]));
  DiodeForward diodeforward_282 (.in(relaydt_2_p28), .out(diodeforward_361_out[2]));
  DiodeForward diodeforward_283 (.in(relaydt_2_p40), .out(diodeforward_361_out[2]));
  DiodeForward diodeforward_284 (.in(relaydt_1_p10), .out(diodeforward_361_out[2]));
  DiodeForward diodeforward_285 (.in(relaydt_2_p5), .out(diodeforward_361_out[2]));
  DiodeForward diodeforward_286 (.in(relaydt_2_p7), .out(diodeforward_361_out[2]));
  DiodeForward diodeforward_287 (.in(relaydt_2_p9), .out(diodeforward_361_out[2]));
  DiodeForward diodeforward_288 (.in(var_dff_with_init_1_p6), .out(diodeforward_361_out[2]));
  DiodeForward diodeforward_289 (.in(relaydt_1_p27), .out(diodeforward_361_out[2]));
  DiodeForward diodeforward_290 (.in(relaydt_1_p29), .out(diodeforward_361_out[2]));
  DiodeForward diodeforward_291 (.in(relaydt_1_p31), .out(diodeforward_361_out[2]));
  DiodeForward diodeforward_292 (.in(relaydt_2_p3), .out(diodeforward_361_out[2]));
  DiodeForward diodeforward_293 (.in(relaydt_1_p11), .out(diodeforward_361_out[2]));
  DiodeForward diodeforward_294 (.in(relaydt_1_p13), .out(diodeforward_361_out[2]));
  DiodeForward diodeforward_295 (.in(relaydt_1_p15), .out(diodeforward_361_out[2]));
  DiodeForward diodeforward_296 (.in(relaydt_1_p25), .out(diodeforward_361_out[2]));
  DiodeForward diodeforward_297 (.in(relaydt_2_p43), .out(diodeforward_361_out[2]));
  DiodeForward diodeforward_298 (.in(var_dff_with_init_1_p13), .out(diodeforward_361_out[2]));
  DiodeForward diodeforward_299 (.in(var_dff_with_init_1_p15), .out(diodeforward_361_out[2]));
  DiodeForward diodeforward_300 (.in(relaydt_1_p9), .out(diodeforward_361_out[2]));
  DiodeForward diodeforward_301 (.in(relaydt_2_p29), .out(diodeforward_361_out[2]));
  DiodeForward diodeforward_302 (.in(relaydt_2_p31), .out(diodeforward_361_out[2]));
  DiodeForward diodeforward_303 (.in(relaydt_2_p33), .out(diodeforward_361_out[2]));
  DiodeForward diodeforward_304 (.in(var_dff_with_init_1_p11), .out(diodeforward_361_out[2]));
  DiodeForward diodeforward_305 (.in(relaydt_2_p41), .out(diodeforward_361_out[2]));
  DiodeForward diodeforward_306 (.in(var_dff_with_init_1_p14), .out(diodeforward_361_out[2]));
  DiodeForward diodeforward_307 (.in(var_dff_with_init_1_p16), .out(diodeforward_361_out[2]));
  DiodeForward diodeforward_308 (.in(relaydt_2_p27), .out(diodeforward_361_out[2]));
  DiodeForward diodeforward_309 (.in(relaydt_2_p26), .out(diodeforward_361_out[2]));
  DiodeForward diodeforward_310 (.in(relaydt_2_p30), .out(diodeforward_361_out[2]));
  DiodeForward diodeforward_311 (.in(var_dff_with_init_1_p10), .out(diodeforward_361_out[2]));
  DiodeForward diodeforward_312 (.in(var_dff_with_init_1_p12), .out(diodeforward_361_out[2]));
  DiodeForward diodeforward_313 (.in(relaydt_2_p24), .out(diodeforward_361_out[2]));
  DiodeForward diodeforward_314 (.in(relaydt_2_p44), .out(diodeforward_361_out[1]));
  DiodeForward diodeforward_315 (.in(relaydt_2_p38), .out(diodeforward_361_out[1]));
  PullDown pulldown_7 (.out(diodeforward_361_out[1]));
  DiodeForward diodeforward_316 (.in(relaydt_2_p2), .out(diodeforward_361_out[1]));
  DiodeForward diodeforward_317 (.in(relaydt_2_p8), .out(diodeforward_361_out[1]));
  DiodeForward diodeforward_318 (.in(relaydt_2_p10), .out(diodeforward_361_out[1]));
  DiodeForward diodeforward_319 (.in(relaydt_2_p16), .out(diodeforward_361_out[1]));
  DiodeForward diodeforward_320 (.in(relaydt_1_p24), .out(diodeforward_361_out[1]));
  DiodeForward diodeforward_321 (.in(relaydt_1_p30), .out(diodeforward_361_out[1]));
  DiodeForward diodeforward_322 (.in(undriven_7), .out(diodeforward_361_out[1]));
  DiodeForward diodeforward_323 (.in(undriven), .out(diodeforward_361_out[1]));
  DiodeForward diodeforward_324 (.in(relaydt_1_p8), .out(diodeforward_361_out[1]));
  DiodeForward diodeforward_325 (.in(relaydt_1_p14), .out(diodeforward_361_out[1]));
  DiodeForward diodeforward_326 (.in(relaydt_1_p16), .out(diodeforward_361_out[1]));
  DiodeForward diodeforward_327 (.in(relaydt_1_p22), .out(diodeforward_361_out[1]));
  DiodeForward diodeforward_328 (.in(var_dff_with_init_1_p2), .out(diodeforward_361_out[1]));
  DiodeForward diodeforward_329 (.in(relaydt_2_p28), .out(diodeforward_361_out[1]));
  DiodeForward diodeforward_330 (.in(relaydt_2_p40), .out(diodeforward_361_out[1]));
  DiodeForward diodeforward_331 (.in(relaydt_1_p6), .out(diodeforward_361_out[1]));
  DiodeForward diodeforward_332 (.in(relaydt_2_p1), .out(diodeforward_361_out[1]));
  DiodeForward diodeforward_333 (.in(relaydt_2_p7), .out(diodeforward_361_out[1]));
  DiodeForward diodeforward_334 (.in(relaydt_2_p9), .out(diodeforward_361_out[1]));
  DiodeForward diodeforward_335 (.in(relaydt_2_p15), .out(diodeforward_361_out[1]));
  DiodeForward diodeforward_336 (.in(relaydt_1_p23), .out(diodeforward_361_out[1]));
  DiodeForward diodeforward_337 (.in(relaydt_1_p29), .out(diodeforward_361_out[1]));
  DiodeForward diodeforward_338 (.in(relaydt_1_p31), .out(diodeforward_361_out[1]));
  DiodeForward diodeforward_339 (.in(undriven_2), .out(diodeforward_361_out[1]));
  DiodeForward diodeforward_340 (.in(relaydt_1_p7), .out(diodeforward_361_out[1]));
  DiodeForward diodeforward_341 (.in(relaydt_1_p13), .out(diodeforward_361_out[1]));
  DiodeForward diodeforward_342 (.in(relaydt_1_p15), .out(diodeforward_361_out[1]));
  DiodeForward diodeforward_343 (.in(relaydt_1_p21), .out(diodeforward_361_out[1]));
  DiodeForward diodeforward_344 (.in(var_dff_with_init_1_p8), .out(diodeforward_361_out[1]));
  DiodeForward diodeforward_345 (.in(var_dff_with_init_1_p13), .out(diodeforward_361_out[1]));
  DiodeForward diodeforward_346 (.in(var_dff_with_init_1_p15), .out(diodeforward_361_out[1]));
  DiodeForward diodeforward_347 (.in(relaydt_1_p5), .out(diodeforward_361_out[1]));
  DiodeForward diodeforward_348 (.in(relaydt_2_p25), .out(diodeforward_361_out[1]));
  DiodeForward diodeforward_349 (.in(relaydt_2_p31), .out(diodeforward_361_out[1]));
  DiodeForward diodeforward_350 (.in(relaydt_2_p33), .out(diodeforward_361_out[1]));
  DiodeForward diodeforward_351 (.in(var_dff_with_init_1_p7), .out(diodeforward_361_out[1]));
  DiodeForward diodeforward_352 (.in(relaydt_2_p42), .out(diodeforward_361_out[1]));
  DiodeForward diodeforward_353 (.in(var_dff_with_init_1_p14), .out(diodeforward_361_out[1]));
  DiodeForward diodeforward_354 (.in(var_dff_with_init_1_p16), .out(diodeforward_361_out[1]));
  DiodeForward diodeforward_355 (.in(relaydt_2_p23), .out(diodeforward_361_out[1]));
  DiodeForward diodeforward_356 (.in(relaydt_2_p22), .out(diodeforward_361_out[1]));
  DiodeForward diodeforward_357 (.in(relaydt_2_p30), .out(diodeforward_361_out[1]));
  DiodeForward diodeforward_358 (.in(var_dff_with_init_1_p10), .out(diodeforward_361_out[1]));
  DiodeForward diodeforward_359 (.in(relaydt_2_p32), .out(diodeforward_361_out[1]));
  DiodeForward diodeforward_360 (.in(var_dff_with_init_1_p9), .out(diodeforward_361_out[1]));
  DiodeForward diodeforward_361 (.in(relaydt_2_p44), .out(diodeforward_361_out[0]));
  DiodeForward diodeforward_362 (.in(var_dff_with_init_1_p3), .out(diodeforward_361_out[0]));
  PullDown pulldown_8 (.out(diodeforward_361_out[0]));
  DiodeForward diodeforward_363 (.in(relaydt_2_p2), .out(diodeforward_361_out[0]));
  DiodeForward diodeforward_364 (.in(relaydt_2_p6), .out(diodeforward_361_out[0]));
  DiodeForward diodeforward_365 (.in(relaydt_2_p10), .out(diodeforward_361_out[0]));
  DiodeForward diodeforward_366 (.in(relaydt_2_p14), .out(diodeforward_361_out[0]));
  DiodeForward diodeforward_367 (.in(relaydt_1_p24), .out(diodeforward_361_out[0]));
  DiodeForward diodeforward_368 (.in(relaydt_1_p28), .out(diodeforward_361_out[0]));
  DiodeForward diodeforward_369 (.in(undriven_7), .out(diodeforward_361_out[0]));
  DiodeForward diodeforward_370 (.in(undriven_3), .out(diodeforward_361_out[0]));
  DiodeForward diodeforward_371 (.in(relaydt_1_p8), .out(diodeforward_361_out[0]));
  DiodeForward diodeforward_372 (.in(relaydt_1_p12), .out(diodeforward_361_out[0]));
  DiodeForward diodeforward_373 (.in(relaydt_1_p16), .out(diodeforward_361_out[0]));
  DiodeForward diodeforward_374 (.in(relaydt_1_p20), .out(diodeforward_361_out[0]));
  DiodeForward diodeforward_375 (.in(var_dff_with_init_1_p2), .out(diodeforward_361_out[0]));
  DiodeForward diodeforward_376 (.in(var_dff_with_init_1_p4), .out(diodeforward_361_out[0]));
  DiodeForward diodeforward_377 (.in(relaydt_2_p40), .out(diodeforward_361_out[0]));
  DiodeForward diodeforward_378 (.in(relaydt_1_p4), .out(diodeforward_361_out[0]));
  DiodeForward diodeforward_379 (.in(relaydt_2_p1), .out(diodeforward_361_out[0]));
  DiodeForward diodeforward_380 (.in(relaydt_2_p5), .out(diodeforward_361_out[0]));
  DiodeForward diodeforward_381 (.in(relaydt_2_p9), .out(diodeforward_361_out[0]));
  DiodeForward diodeforward_382 (.in(relaydt_2_p13), .out(diodeforward_361_out[0]));
  DiodeForward diodeforward_383 (.in(relaydt_1_p23), .out(diodeforward_361_out[0]));
  DiodeForward diodeforward_384 (.in(relaydt_1_p27), .out(diodeforward_361_out[0]));
  DiodeForward diodeforward_385 (.in(relaydt_1_p31), .out(diodeforward_361_out[0]));
  DiodeForward diodeforward_386 (.in(undriven_4), .out(diodeforward_361_out[0]));
  DiodeForward diodeforward_387 (.in(relaydt_1_p7), .out(diodeforward_361_out[0]));
  DiodeForward diodeforward_388 (.in(relaydt_1_p11), .out(diodeforward_361_out[0]));
  DiodeForward diodeforward_389 (.in(relaydt_1_p15), .out(diodeforward_361_out[0]));
  DiodeForward diodeforward_390 (.in(relaydt_1_p19), .out(diodeforward_361_out[0]));
  DiodeForward diodeforward_391 (.in(var_dff_with_init_1_p8), .out(diodeforward_361_out[0]));
  DiodeForward diodeforward_392 (.in(relaydt_2_p43), .out(diodeforward_361_out[0]));
  DiodeForward diodeforward_393 (.in(var_dff_with_init_1_p15), .out(diodeforward_361_out[0]));
  DiodeForward diodeforward_394 (.in(relaydt_1_p3), .out(diodeforward_361_out[0]));
  DiodeForward diodeforward_395 (.in(relaydt_2_p25), .out(diodeforward_361_out[0]));
  DiodeForward diodeforward_396 (.in(relaydt_2_p29), .out(diodeforward_361_out[0]));
  DiodeForward diodeforward_397 (.in(relaydt_2_p33), .out(diodeforward_361_out[0]));
  DiodeForward diodeforward_398 (.in(relaydt_2_p37), .out(diodeforward_361_out[0]));
  DiodeForward diodeforward_399 (.in(relaydt_2_p42), .out(diodeforward_361_out[0]));
  DiodeForward diodeforward_400 (.in(relaydt_2_p41), .out(diodeforward_361_out[0]));
  DiodeForward diodeforward_401 (.in(var_dff_with_init_1_p16), .out(diodeforward_361_out[0]));
  DiodeForward diodeforward_402 (.in(relaydt_2_p21), .out(diodeforward_361_out[0]));
  DiodeForward diodeforward_403 (.in(relaydt_2_p22), .out(diodeforward_361_out[0]));
  DiodeForward diodeforward_404 (.in(relaydt_2_p26), .out(diodeforward_361_out[0]));
  DiodeForward diodeforward_405 (.in(var_dff_with_init_1_p10), .out(diodeforward_361_out[0]));
  DiodeForward diodeforward_406 (.in(relaydt_2_p36), .out(diodeforward_361_out[0]));
  DiodeForward diodeforward_407 (.in(relaydt_2_p18), .out(diodeforward_361_out[0]));

  // Notes on the sheet:
  //   clk: Hz: 10000
endmodule
