// Digital circuit no bits (nor).dig as structural Verilog
module no_bits__nor (
  input  [3:0] d_n,
  output \nor 
);

  wire [7:4] undriven;

  // NOr nor_1 has open pins: In_1={undriven, d_n}, In_2=open, out=open
endmodule

/* Code that sets the parameters or builds the circuit:
addWire(4,0,4,args.bits/2);
*/

/* Code that sets the parameters or builds the circuit:
bits := 16;
*/
