// Digital circuit var DFF with init.dig as structural Verilog
module var_DFF_with_init (
  input  [15:0] D,
  input  clk,
  output [15:0] Q,
  output [15:0] nQ
);

  wire diodeforward_1_out, edge_pulse_detector_1_plus, or_1_out, reset_1_out;
  wire [15:0] driver_1_out;

  Reset reset_1 (.out(reset_1_out));
  or or_1 (or_1_out, reset_1_out, or_1_out);
  edge_pulse_detector edge_pulse_detector_1 (.clk(or_1_out), .plus(edge_pulse_detector_1_plus));
  DiodeForward diodeforward_1 (.in(clk), .out(diodeforward_1_out));
  PullDown pulldown_1 (.out(diodeforward_1_out));
  DiodeForward diodeforward_2 (.in(edge_pulse_detector_1_plus), .out(diodeforward_1_out));
  assign driver_1_out = or_1_out ? D : 16'bz;  // Driver driver_1
  assign driver_1_out = ~or_1_out ? 16'h1 : 16'bz;  // DriverInvSel driverinvsel_1
  var_DFF #(.generic("bits := args.bits;")) var_dff_1 (.D(driver_1_out), .clk(diodeforward_1_out), .Q(Q), .nQ(nQ));
endmodule

/* Code that sets the parameters or builds the circuit:
bits := 16;
init := 0xFE;
*/
