// Digital circuit var DFF.dig as structural Verilog
module var_DFF (
  input  D,
  input  clk,
  output Q,
  output nQ
);

  wire nand_1_out, nand_2_out, nand_3_out, nand_4_out, nand_5_out, nand_6_out, reset_1_out, reset_2_out;

  nand nand_1 (nand_1_out, ~clk, D);  // NAnd
  nand nand_2 (nand_2_out, ~D, ~clk);  // NAnd
  nand nand_3 (nand_3_out, nand_1_out, nand_4_out);
  nand nand_4 (nand_4_out, nand_3_out, reset_1_out, nand_2_out);
  Reset reset_1 (.out(reset_1_out));
  nand nand_5 (nand_5_out, clk, nand_3_out);
  nand nand_6 (nand_6_out, nand_4_out, clk);
  nand nand_7 (Q, nand_5_out, nQ);
  nand nand_8 (nQ, Q, reset_2_out, nand_6_out);
  Reset reset_2 (.out(reset_2_out));
endmodule

/* Code that sets the parameters or builds the circuit:
bits:=16;
*/
