// Digital circuit var adder.dig as structural Verilog
module var_adder (
  input  [7:0] A,
  input  [7:0] B,
  input  c_i,
  output [7:0] out_4,
  output c_o
);

  PullDown #(.generic("bits := 8; if (isPresent(args.bits)) { bits = args.bits; } this.Bits = bits;")) pulldown_1 (.out(A));
  PullDown #(.generic("bits := 8; if (isPresent(args.bits)) { bits = args.bits; } this.Bits = bits;")) pulldown_2 (.out(B));
  PullDown pulldown_3 (.out(c_i));
endmodule

/* Code that sets the parameters or builds the circuit:
bits := 8;
if (isPresent(args.bits)) {
  bits = args.bits;
}

func addHalfAdder(x,y) {
addComponent("XOr",x+3,y);
addComponent("And",x+3,y+3);
addWire(x,y,x+3,y);
addWire(x,y+2,x+3,y+2);
addWire(x+2,y,x+2,y+3);
addWire(x+1,y+2,x+1,y+5);
addWire(x+2,y+3,x+3,y+3);
addWire(x+1,y+5,x+3,y+5);
addWire(x+6,y+1,x+7,y+1);
addWire(x+6,y+4,x+7,y+4);

}

func addFullAdder(x,y) {

addHalfAdder(x,y);
addHalfAdder(x+7,y-1);
addComponent("Or",x+14,y+3);
addWire(x+7,y+4,x+7,y+5);
addWire(x+7,y+5,x+14,y+5);
addWire(x+14,y,x+18,y);
addWire(x+17,y+4,x+18,y+4);

}

for (i:=0;i<bits;i++) {

addFullAdder(1,i*8);
if (i<bits-1) {
addWire(19,i*8+4,19,i*8+6);
addWire(8,i*8+6,19,i*8+6);
addWire(8,i*8+6,8,i*8+7);
} else {
addWire(18,i*8+4,20,i*8+4);
addWire(20,i*8+4,20,1);
addWire(20,1,21,1);
}

}
*/

/* Code that sets the parameters or builds the circuit:
bits := 9;
*/
