// Digital circuit var reg with init.dig as structural Verilog
module var_reg_with_init (
  input  RE,
  input  WE,
  input  [15:0] D,
  input  C,
  output [15:0] Q
);

  wire and_1_out, edge_pulse_detector_1_plus;

  and and_1 (and_1_out, WE, edge_pulse_detector_1_plus);
  edge_pulse_detector edge_pulse_detector_1 (.clk(C), .plus(edge_pulse_detector_1_plus));
  var_DFF_with_init #(.generic("bits := args.bits; init := args.init;")) var_dff_with_init_1 (
    .D(D), .clk(and_1_out), .Q(Q));  // open: nQ
  assign D = RE ? Q : 16'bz;  // Driver driver_1
endmodule

/* Code that sets the parameters or builds the circuit:
bits := 16;
init := 123;
*/
