// Digital circuit var ring counter with reset.dig as structural Verilog
module var_ring_counter_with_reset (
  input  C,
  input  R
);

  wire or_1_out, pulldown_1_out, undriven;

  PullDown pulldown_1 (.out(pulldown_1_out));
  or or_1 (or_1_out, pulldown_1_out, undriven);

  // Notes on the sheet:
  //   C: Hz: 10
endmodule

/* Code that sets the parameters or builds the circuit:
size := 4;
*/

/* Code that sets the parameters or builds the circuit:
size := args.size;

for(i:=0;i<size;i++) {
  x := i*7;
  addComponent("var DFF.dig",x,0).bits := 1;
  addComponent("DriverInvSel",x-3,0);
  fet := addComponent("PFET",x+2,-1);
  fet.rotation = 1;
  fet.unidirectional = true;
  fet.mirror = true;
  if (i = 0) {
    addComponent("PullUp",x-1,-1);
  } else {
    addComponent("PullDown",x-1,-1).rotation = 2;
  }
  addWire(x-2,0,x,0);
  addWire(x-1,0,x-1,-1);
  addWire(x+2,0,x+2,-1);
  addWire(x-1,1,x,1);
  addWire(x-1,1,x-1,2);
  addWire(x-3,-1,x-3,-3);
  addWire(x+2,0,x+3,0);
  addWire(x,-2,x-5,-2);
  addWire(x+3,0,x+3,5);
  out := addComponent("Out",x+3,5);
  out.rotation = 3;
  out.Label = "o_" + i;
  if (i = 0) {
    addWire(x-1,2,x-10,2);
  } else {
    addWire(x-1,2,x-8,2);
  }
  addWire(x-3,-3,x-10,-3);
  if (i = size-1) {
    addComponent("VDD",x+2,-3);
    addWire(x+2,-3,x+2,-2);
  }
}

addWire(-9,3,-4+size*7,3);
*/
